// Logisim project 4bit.circ as structural Verilog: 2 circuits, main circuit main
module main (
  input  [3:0] A,
  input  [3:0] B,
  input  Cin,
  output Cout,
  output [3:0] S
);

  wire onebit_1_out_5, onebit_2_out_5, onebit_3_out_5;

  onebit onebit_1 (.in_1(A[0]), .in_2(B[0]), .in_3(Cin), .out_4(S[0]), .out_5(onebit_1_out_5));
  onebit onebit_2 (.in_1(A[1]), .in_2(B[1]), .in_3(onebit_1_out_5), .out_4(S[1]), .out_5(onebit_2_out_5));
  onebit onebit_3 (.in_1(A[2]), .in_2(B[2]), .in_3(onebit_2_out_5), .out_4(S[2]), .out_5(onebit_3_out_5));
  onebit onebit_4 (.in_1(A[3]), .in_2(B[3]), .in_3(onebit_3_out_5), .out_4(S[3]), .out_5(Cout));
endmodule

module onebit (
  input  in_1,
  input  in_2,
  input  in_3,
  output out_4,
  output out_5
);

  wire and_1_out, and_2_out, xor_1_out;

  xor xor_1 (xor_1_out, in_1, in_2);
  xor xor_2 (out_4, xor_1_out, in_3);
  and and_1 (and_1_out, xor_1_out, in_3);
  and and_2 (and_2_out, in_1, in_2);
  or or_1 (out_5, and_1_out, and_2_out);
endmodule
