// Logisim project 7segment.circ as structural Verilog: 1 circuit, main circuit main
module main (
  input  a,
  input  b,
  input  c,
  input  d
);

  wire and_1_out, and_2_out, and_3_out, and_4_out, and_5_out, and_6_out, and_7_out, and_8_out, and_9_out,
       and_10_out, and_11_out, and_12_out, and_13_out, and_14_out, not_1_out, not_2_out, not_3_out,
       not_4_out, not_5_out, not_6_out, not_7_out, not_8_out, not_9_out, not_10_out, not_11_out, not_12_out,
       not_13_out, not_14_out, not_15_out, not_16_out, not_17_out, not_18_out, not_19_out, not_20_out,
       or_1_out, or_2_out, or_3_out, or_4_out, or_5_out, or_6_out, or_7_out, xor_1_out;

  not not_1 (not_1_out, b);
  xor xor_1 (xor_1_out, c, not_2_out);
  not not_2 (not_2_out, d);
  not not_3 (not_3_out, b);
  and and_1 (and_1_out, not_3_out, not_4_out);
  not not_4 (not_4_out, d);
  and and_2 (and_2_out, c, not_5_out);
  not not_5 (not_5_out, d);
  not not_6 (not_6_out, b);
  and and_3 (and_3_out, not_6_out, not_7_out);
  not not_7 (not_7_out, d);
  and and_4 (and_4_out, b, d);
  not not_8 (not_8_out, c);
  or or_1 (or_1_out, not_8_out, d, b);
  not not_9 (not_9_out, b);
  and and_5 (and_5_out, not_9_out, not_10_out);
  not not_10 (not_10_out, d);
  not not_11 (not_11_out, b);
  and and_6 (and_6_out, not_11_out, c);
  and and_7 (and_7_out, c, not_12_out);
  not not_12 (not_12_out, d);
  and and_8 (and_8_out, b, not_13_out, d);
  not not_13 (not_13_out, c);
  not not_14 (not_14_out, b);
  and and_9 (and_9_out, not_14_out, c);
  and and_10 (and_10_out, b, not_15_out);
  not not_15 (not_15_out, c);
  and and_11 (and_11_out, b, not_16_out);
  not not_16 (not_16_out, d);
  not not_17 (not_17_out, c);
  and and_12 (and_12_out, not_17_out, not_18_out);
  not not_18 (not_18_out, d);
  and and_13 (and_13_out, b, not_19_out);
  not not_19 (not_19_out, c);
  and and_14 (and_14_out, b, not_20_out);
  not not_20 (not_20_out, d);
  or or_2 (or_2_out, not_1_out, xor_1_out);
  or or_3 (or_3_out, and_1_out, and_2_out);
  or or_4 (or_4_out, and_3_out, c, and_4_out, a);
  or or_5 (or_5_out, and_5_out, and_6_out, and_7_out, and_8_out, a);
  or or_6 (or_6_out, and_9_out, and_10_out, and_11_out, a);
  or or_7 (or_7_out, and_12_out, and_13_out, and_14_out, a);
  _7_Segment_Display u_7_segment_display_1 (
    .g(or_6_out), .f(or_7_out), .a(or_4_out), .b(or_2_out), .e(or_3_out), .d(or_5_out), .c(or_1_out));  // open: dp
endmodule
