// Logisim project ALU_template.circ as structural Verilog: 10 circuits, main circuit ALU32
module LeftShift32 (
  input  [31:0] B,
  input  [4:0] Sa,
  input  Cin,
  output [31:0] C
);

  wire [31:0] multiplexer_1_out, multiplexer_2_out, multiplexer_3_out, multiplexer_4_out;

  Multiplexer #(.width(32), .enable("false")) multiplexer_1 (
    .in0(B), .in1({B[15:0], {16{Cin}}}), .out(multiplexer_1_out), .sel(Sa[4]));
  Multiplexer #(.width(32), .enable("false")) multiplexer_2 (
    .in0(multiplexer_1_out), .in1({multiplexer_1_out[23:0], {8{Cin}}}), .out(multiplexer_2_out), .sel(Sa[3]));
  Multiplexer #(.width(32), .enable("false")) multiplexer_3 (
    .in0(multiplexer_2_out), .in1({multiplexer_2_out[27:0], {4{Cin}}}), .out(multiplexer_3_out), .sel(Sa[2]));
  Multiplexer #(.width(32), .enable("false")) multiplexer_4 (
    .in0(multiplexer_3_out), .in1({multiplexer_3_out[29:0], {2{Cin}}}), .out(multiplexer_4_out), .sel(Sa[1]));
  Multiplexer #(.width(32), .enable("false")) multiplexer_5 (
    .in0(multiplexer_4_out), .in1({multiplexer_4_out[30:0], Cin}), .out(C), .sel(Sa[0]));
endmodule

module Add32 (
  input  [31:0] A,
  input  [31:0] B,
  input  Cin,
  output [31:0] C,
  output V
);

  wire onebit_1_cout, onebit_2_cout, onebit_3_cout, onebit_4_cout, sixteenbitadder_1_cout, twelvebit_1_cout;

  sixteenbitadder sixteenbitadder_1 (.A(A[15:0]), .B(B[15:0]), .Cin(Cin), .Cout(sixteenbitadder_1_cout), .Sum(C[15:0]));
  twelvebit twelvebit_1 (
    .A(A[27:16]), .B(B[27:16]), .Cin(sixteenbitadder_1_cout), .Cout(twelvebit_1_cout), .Sum(C[27:16]));
  onebit onebit_1 (.A(A[28]), .B(B[28]), .Cin(twelvebit_1_cout), .Sum(C[28]), .Cout(onebit_1_cout));
  onebit onebit_2 (.A(A[29]), .B(B[29]), .Cin(onebit_1_cout), .Sum(C[29]), .Cout(onebit_2_cout));
  onebit onebit_3 (.A(A[30]), .B(B[30]), .Cin(onebit_2_cout), .Sum(C[30]), .Cout(onebit_3_cout));
  onebit onebit_4 (.A(A[31]), .B(B[31]), .Cin(onebit_3_cout), .Sum(C[31]), .Cout(onebit_4_cout));
  onebit onebit_5 (.A(A[31]), .B(B[31]), .Cin(onebit_3_cout), .Sum(C[31]), .Cout(onebit_4_cout));
  xor xor_1 (V, onebit_4_cout, onebit_3_cout);
endmodule

module ALU32 (
  input  [31:0] A,
  input  [31:0] B,
  input  [3:0] Op,
  input  [4:0] Sa,
  output [31:0] C,
  output V
);

  wire add32_1_v, not_1_out;
  wire [31:0] add32_1_c, bit_extender_1_out, eqnegtle_1_c, multiplexer_1_out, multiplexer_2_out,
       ornorandxor_1_c, shifts_1_c, xor_1_out;

  assign bit_extender_1_out = {{31{Op[2]}}, Op[2]};  // Bit_Extender bit_extender_1
  OrNorAndXor ornorandxor_1 (.A(A), .B(B), .Op1(Op[1]), .Op2(Op[2]), .C(ornorandxor_1_c));
  assign xor_1_out = B ^ bit_extender_1_out;  // XOR_Gate xor_1, 32 bits wide
  EqNeGtLe eqnegtle_1 (.Op2(Op[2]), .Op1(Op[1]), .A(A), .B(B), .C(eqnegtle_1_c));
  Add32 add32_1 (.A(A), .B(xor_1_out), .Cin(Op[2]), .C(add32_1_c), .V(add32_1_v));
  shifts shifts_1 (.Op2(Op[2]), .Op0(Op[0]), .A(A), .Sa(Sa), .C(shifts_1_c));
  Multiplexer #(.width(32), .enable("false")) multiplexer_1 (
    .in0(eqnegtle_1_c), .in1(ornorandxor_1_c), .out(multiplexer_1_out), .sel(Op[0]));
  Multiplexer #(.width(32), .enable("false")) multiplexer_2 (
    .in0(add32_1_c), .in1(shifts_1_c), .out(multiplexer_2_out), .sel(Op[1]));
  Multiplexer #(.width(32), .enable("false")) multiplexer_3 (
    .in0(multiplexer_1_out), .in1(multiplexer_2_out), .out(C), .sel(Op[3]));
  not not_1 (not_1_out, Op[1]);
  and and_1 (V, Op[3], not_1_out, add32_1_v);
endmodule

module fourbit (
  input  [3:0] A,
  input  [3:0] B,
  input  Cin,
  output Cout,
  output [3:0] Sum
);

  wire onebit_1_cout, onebit_2_cout, onebit_3_cout;

  onebit onebit_1 (.A(A[0]), .B(B[0]), .Cin(Cin), .Sum(Sum[0]), .Cout(onebit_1_cout));
  onebit onebit_2 (.A(A[1]), .B(B[1]), .Cin(onebit_1_cout), .Sum(Sum[1]), .Cout(onebit_2_cout));
  onebit onebit_3 (.A(A[2]), .B(B[2]), .Cin(onebit_2_cout), .Sum(Sum[2]), .Cout(onebit_3_cout));
  onebit onebit_4 (.A(A[3]), .B(B[3]), .Cin(onebit_3_cout), .Sum(Sum[3]), .Cout(Cout));
endmodule

module onebit (
  input  A,
  input  B,
  input  Cin,
  output Sum,
  output Cout
);

  wire and_1_out, and_2_out, xor_1_out;

  xor xor_1 (xor_1_out, A, B);
  xor xor_2 (Sum, xor_1_out, Cin);
  and and_1 (and_1_out, xor_1_out, Cin);
  and and_2 (and_2_out, A, B);
  or or_1 (Cout, and_1_out, and_2_out);
endmodule

module sixteenbitadder (
  input  [15:0] A,
  input  [15:0] B,
  input  Cin,
  output Cout,
  output [15:0] Sum
);

  wire fourbit_1_cout, fourbit_2_cout, fourbit_3_cout;

  fourbit fourbit_1 (.A(A[3:0]), .B(B[3:0]), .Cin(Cin), .Cout(fourbit_1_cout), .Sum(Sum[3:0]));
  fourbit fourbit_2 (.A(A[7:4]), .B(B[7:4]), .Cin(fourbit_1_cout), .Cout(fourbit_2_cout), .Sum(Sum[7:4]));
  fourbit fourbit_3 (.A(A[11:8]), .B(B[11:8]), .Cin(fourbit_2_cout), .Cout(fourbit_3_cout), .Sum(Sum[11:8]));
  fourbit fourbit_4 (.A(A[15:12]), .B(B[15:12]), .Cin(fourbit_3_cout), .Cout(Cout), .Sum(Sum[15:12]));
endmodule

module twelvebit (
  input  [11:0] A,
  input  [11:0] B,
  input  Cin,
  output Cout,
  output [11:0] Sum
);

  wire fourbit_1_cout, fourbit_2_cout;

  fourbit fourbit_1 (.A(A[3:0]), .B(B[3:0]), .Cin(Cin), .Cout(fourbit_1_cout), .Sum(Sum[3:0]));
  fourbit fourbit_2 (.A(A[7:4]), .B(B[7:4]), .Cin(fourbit_1_cout), .Cout(fourbit_2_cout), .Sum(Sum[7:4]));
  fourbit fourbit_3 (.A(A[11:8]), .B(B[11:8]), .Cin(fourbit_2_cout), .Cout(Cout), .Sum(Sum[11:8]));
endmodule

module OrNorAndXor (
  input  [31:0] A,
  input  [31:0] B,
  input  Op1,
  input  Op2,
  output [31:0] C
);

  wire [31:0] and_1_out, nor_1_out, or_1_out, xor_1_out;

  assign or_1_out = A | B;  // OR_Gate or_1, 32 bits wide
  assign and_1_out = A & B;  // AND_Gate and_1, 32 bits wide
  assign nor_1_out = ~(A | B);  // NOR_Gate nor_1, 32 bits wide
  assign xor_1_out = A ^ B;  // XOR_Gate xor_1, 32 bits wide
  Multiplexer #(.select(2), .width(32), .enable("false")) multiplexer_1 (
    .in0(or_1_out), .in1(and_1_out), .in2(nor_1_out), .in3(xor_1_out), .out(C), .sel({Op2, Op1}));
endmodule

module EqNeGtLe (
  input  Op2,
  input  Op1,
  input  [31:0] A,
  input  [31:0] B,
  output [31:0] C
);

  wire and_1_out, and_2_out, multiplexer_1_out, or_1_out, xnor_2_out, xor_1_out;
  wire [30:0] not_1_out;
  wire [31:0] xnor_1_out;

  assign not_1_out = ~A[30:0];  // NOT_Gate not_1, 31 bits wide
  assign xnor_1_out = ~(A ^ B);  // XNOR_Gate xnor_1, 32 bits wide
  and and_1 (and_1_out, not_1_out[0], not_1_out[1], not_1_out[2], not_1_out[3], not_1_out[4], not_1_out[5], not_1_out[6], not_1_out[7], not_1_out[8], not_1_out[9], not_1_out[10], not_1_out[11], not_1_out[12], not_1_out[13], not_1_out[14], not_1_out[15], not_1_out[16], not_1_out[17], not_1_out[18], not_1_out[19], not_1_out[20], not_1_out[21], not_1_out[22], not_1_out[23], not_1_out[24], not_1_out[25], not_1_out[26], not_1_out[27], not_1_out[28], not_1_out[29], not_1_out[30]);
  and and_2 (and_2_out, xnor_1_out[0], xnor_1_out[1], xnor_1_out[2], xnor_1_out[3], xnor_1_out[4], xnor_1_out[5], xnor_1_out[6], xnor_1_out[7], xnor_1_out[8], xnor_1_out[9], xnor_1_out[10], xnor_1_out[11], xnor_1_out[12], xnor_1_out[13], xnor_1_out[14], xnor_1_out[15], xnor_1_out[17], xnor_1_out[18], xnor_1_out[19], xnor_1_out[20], xnor_1_out[21], xnor_1_out[22], xnor_1_out[23], xnor_1_out[24], xnor_1_out[25], xnor_1_out[26], xnor_1_out[27], xnor_1_out[28], xnor_1_out[29], xnor_1_out[30], xnor_1_out[31]);
  or or_1 (or_1_out, and_1_out, A[31]);
  xor xor_1 (xor_1_out, Op1, or_1_out);
  xnor xnor_2 (xnor_2_out, Op1, and_2_out);
  Multiplexer #(.enable("false")) multiplexer_1 (.in0(xnor_2_out), .in1(xor_1_out), .out(multiplexer_1_out), .sel(Op2));
  assign C = {{31{1'b0}}, multiplexer_1_out};  // Bit_Extender bit_extender_1
endmodule

module shifts (
  input  Op2,
  input  Op0,
  input  [31:0] A,
  input  [4:0] Sa,
  output [31:0] C
);

  wire and_1_out, and_2_out;
  wire [31:0] leftshift32_1_c, multiplexer_1_out;

  Multiplexer #(.width(32), .enable("false")) multiplexer_1 (
    .in0(A),
    .in1({A[0], A[1], A[2], A[3], A[4], A[5], A[6], A[7], A[8], A[9], A[10], A[11], A[12], A[13], A[14], A[15], A[16], A[17], A[18], A[19], A[20], A[21], A[22], A[23], A[24], A[25], A[26], A[27], A[28], A[29], A[30], A[31]}),
    .out(multiplexer_1_out), .sel(Op2));
  and and_1 (and_1_out, Op0, Op2);
  and and_2 (and_2_out, and_1_out, A[31]);
  LeftShift32 leftshift32_1 (.B(multiplexer_1_out), .Sa(Sa), .Cin(and_2_out), .C(leftshift32_1_c));
  Multiplexer #(.width(32), .enable("false")) multiplexer_2 (
    .in0(leftshift32_1_c),
    .in1({leftshift32_1_c[0], leftshift32_1_c[1], leftshift32_1_c[2], leftshift32_1_c[3], leftshift32_1_c[4], leftshift32_1_c[5], leftshift32_1_c[6], leftshift32_1_c[7], leftshift32_1_c[8], leftshift32_1_c[9], leftshift32_1_c[10], leftshift32_1_c[11], leftshift32_1_c[12], leftshift32_1_c[13], leftshift32_1_c[14], leftshift32_1_c[15], leftshift32_1_c[16], leftshift32_1_c[17], leftshift32_1_c[18], leftshift32_1_c[19], leftshift32_1_c[20], leftshift32_1_c[21], leftshift32_1_c[22], leftshift32_1_c[23], leftshift32_1_c[24], leftshift32_1_c[25], leftshift32_1_c[26], leftshift32_1_c[27], leftshift32_1_c[28], leftshift32_1_c[29], leftshift32_1_c[30], leftshift32_1_c[31]}),
    .out(C), .sel(Op2));
endmodule
