// Logisim project RISCV.circ as structural Verilog: 2 circuits, main circuit main
module main (
);

  wire clock_1_out, registerfile_1_p1, registerfile_1_p2, registerfile_1_p3, registerfile_1_p6,
       registerfile_1_p7, risc_vprogramrom_1_p1, risc_vprogramrom_1_p3, risc_vprogramrom_1_p4;
  wire [1:0] incrementer_1_p7;
  wire [31:0] incrementer_1_p3, incrementer_1_p5, incrementer_1_p6, multiplexer_1_out, register_1_q;

  Register #(.width(32)) register_1 (.D(multiplexer_1_out), .clk(clock_1_out), .Q(register_1_q));  // open: en, clr
  Clock clock_1 (.out(clock_1_out));
  Multiplexer #(.select(2), .width(32), .enable("false")) multiplexer_1 (
    .in0(incrementer_1_p3), .in1(incrementer_1_p5), .in2(incrementer_1_p6), .out(multiplexer_1_out),
    .sel(incrementer_1_p7));  // open: in3
  // Incrementer #(.width(32)) incrementer_1: pin names not known; wires that end beside it: clock_1_out, register_1_q, incrementer_1_p3, register_1_q, incrementer_1_p5, incrementer_1_p6, incrementer_1_p7
  // RISC_VProgramROM risc_vprogramrom_1: pin names not known; wires that end beside it: risc_vprogramrom_1_p1, risc_vprogramrom_1_p1, risc_vprogramrom_1_p3, risc_vprogramrom_1_p4
  // RegisterFile registerfile_1: pin names not known; wires that end beside it: registerfile_1_p1, registerfile_1_p2, registerfile_1_p3, risc_vprogramrom_1_p3, risc_vprogramrom_1_p4, registerfile_1_p6, registerfile_1_p7, registerfile_1_p3, registerfile_1_p2, registerfile_1_p1, registerfile_1_p6, registerfile_1_p7, incrementer_1_p3
endmodule

module Decode (
  input  [31:0] inst
);
endmodule
