// Logisim project RISCV.circ as structural Verilog: 5 circuits, main circuit main
module main (
);

  Fetch fetch_1 ();  // open: Op, pcplus4, out_3
  Register #(.width(32)) register_1 ();  // open: D, en, Q, clk, clr
endmodule

module Decode (
  input  [31:0] w,
  input  WE,
  input  [31:0] xW,
  input  [31:0] inst,
  input  [31:0] PCplus4,
  output [31:0] xA,
  output [31:0] xB
);

  wire registerfile_1_p1, registerfile_1_p2;

  // RegisterFile registerfile_1: pin names not known; wires that end beside it: registerfile_1_p1, registerfile_1_p2, w, WE, xW, registerfile_1_p1, registerfile_1_p2, xA, xB
endmodule

module Fetch (
  output [31:0] Op,
  output [31:0] pcplus4,
  output out_3
);

  wire [29:0] register_1_q;

  Register #(.width(32)) register_1 (.D(pcplus4), .clk(out_3), .Q({register_1_q, pcplus4[1:0]}));  // open: en, clr
  Clock clock_1 (.out(out_3));
  // Incrementer #(.width(30)) incrementer_1: pin names not known; wires that end beside it: out_3, register_1_q, pcplus4[31:2], {register_1_q, pcplus4[1:0]}
  // RISC_VProgramROM risc_vprogramrom_1: pin names not known; wires that end beside it: Op
endmodule

module instdecode (
  input  [31:0] inst,
  output [4:0] xA,
  output [4:0] xB,
  output [19:0] imm,
  output [14:0] control
);
endmodule

module decodetoop (
  input  [2:0] in_1,
  input  in_2,
  output [3:0] out_3
);

  wire and_1_out, and_2_out, nand_1_out, nor_1_out, nor_2_out, not_1_out, not_2_out, not_3_out, not_4_out,
       or_4_out, xor_1_out;

  and and_1 (and_1_out, in_2, in_1[0], not_1_out);
  not not_1 (not_1_out, in_1[1]);
  not not_2 (not_2_out, in_1[2]);
  or or_1 (out_3[0], and_1_out, not_2_out);
  not not_3 (not_3_out, in_1[0]);
  and and_2 (and_2_out, not_3_out, in_1[2]);
  xor xor_1 (xor_1_out, in_1[1], in_1[2]);
  nor nor_1 (nor_1_out, in_1[0], in_1[1], in_1[2], not_4_out);
  not not_4 (not_4_out, in_2);
  or or_2 (out_3[3], and_2_out, in_1[1]);
  nor nor_2 (nor_2_out, in_1[2], in_1[0]);
  nand nand_1 (nand_1_out, in_1[0], in_1[2]);
  or or_3 (out_3[2], xor_1_out, nor_1_out);
  or or_4 (or_4_out, in_1[1], nor_2_out);
  and and_3 (out_3[1], or_4_out, nand_1_out);
endmodule
