// Logisim project RISCV.circ as structural Verilog: 13 circuits, main circuit RISCV32
module RISCV32 (
  output [31:0] out_1,
  output [19:0] out_2,
  output [3:0] out_3,
  output [3:0] out_4
);

  wire and_1_out, and_5_out, AUIPC_q, bctrl_1_branchctrl, bypass_black_box_1_p3, clk,
       comparator_black_box_1_p4, comparator_black_box_1_p5, comparator_black_box_1_p6, DE_EX_regWE_q,
       DE_EX_set_q, DE_EX_shiftreg_q, DE_EX_useImm_q, decode_1_auipc, decode_1_hasrs2, decode_1_regwe,
       decode_1_set, decode_1_setsign, decode_1_shiftbyregval, decode_1_useimm, decode_1_zeroouta, M_W_ld_q,
       nor_1_out, not_1_out, not_2_out, or_1_out, or_2_out, or_3_out, ramctrl_1_ld, ramctrl_1_str,
       registerfile_1_p3, set_signed_q, stallctrl_1_stall, ZeroOutA_q;
  wire [1:0] bypass_black_box_1_p7, bypass_black_box_1_p8, ramctrl_1_lb_ctrl;
  wire [3:0] and_6_out, bit_extender_4_out, DE_EX_ALUop_q, DE_EX_MemHot_q, decode_1_aluop, decode_1_memhot;
  wire [4:0] and_4_out, bit_extender_3_out, bypass_black_box_1_p4, DE_EX_rd_q, decode_1_rd, decode_1_rs1,
       decode_1_rs2, registerfile_1_p4, rs1_q, rs2_q;
  wire [31:0] and_2_out, and_3_out, bit_extender_1_out, bit_extender_2_out, datactrl_1_dout, DE_EX_A_q,
       DE_EX_B_q, DE_EX_imm_q, DE_EX_PC_q, decode_1_imm, decode_1_onehot, EX_M_Result_q, execute_1_result,
       IF_DE_instr_q, increment_pc_1_out_2, M_W_Data_q, M_W_Result_q, multiplexer_1_out, multiplexer_2_out,
       multiplexer_3_out, multiplexer_4_out, multiplexer_5_out, multiplexer_6_out, mux3to1_1_out_5,
       mux3to1_2_out_5, OneHot_q, PC_q, PCplus4_q, PCplus4ex_q, ram_1_p7, ramctrl_1_b_out, register_1_q,
       registerfile_1_p1, registerfile_1_p7, registerfile_1_p8, risc_vprogramrom_1_p2, zapinst_1_nopinst;

  Clock clock_1 (.out(clk));
  Register #(.width(32)) register_1 (.D(multiplexer_1_out), .en(not_2_out), .clk(clk), .Q(register_1_q));  // open: clr
  Multiplexer #(.width(32), .enable("false")) multiplexer_1 (
    .in0(increment_pc_1_out_2), .in1(execute_1_result), .out(multiplexer_1_out), .sel(or_3_out));
  // RISC_VProgramROM risc_vprogramrom_1: pin names not known; wires that end beside it: register_1_q, risc_vprogramrom_1_p2
  Increment_PC increment_pc_1 (.in_1(register_1_q), .out_2(increment_pc_1_out_2));
  Register #(.width(32)) IF_DE_instr (
    .D(multiplexer_2_out), .en(not_2_out), .clk(clk), .Q(IF_DE_instr_q));  // open: clr
  Multiplexer #(.width(32), .enable("false")) multiplexer_2 (
    .in0(risc_vprogramrom_1_p2), .in1(zapinst_1_nopinst), .out(multiplexer_2_out), .sel(or_3_out));
  Register #(.width(32)) PC (.D(register_1_q), .en(not_2_out), .clk(clk), .Q(PC_q));  // open: clr
  ZapInst zapinst_1 (.Zap(or_3_out), .Nopinst(zapinst_1_nopinst));
  Register #(.width(32)) PCplus4 (.D(increment_pc_1_out_2), .en(not_2_out), .clk(clk), .Q(PCplus4_q));  // open: clr
  Multiplexer #(.width(32), .enable("false")) multiplexer_3 (
    .in0(IF_DE_instr_q), .in1(zapinst_1_nopinst), .out(multiplexer_3_out), .sel(or_3_out));
  not not_1 (not_1_out, clk);
  Decode decode_1 (
    .instr(multiplexer_3_out), .rs1(decode_1_rs1), .rs2(decode_1_rs2), .rd(decode_1_rd), .imm(decode_1_imm),
    .useImm(decode_1_useimm), .ALUop(decode_1_aluop), .onehot(decode_1_onehot), .regWE(decode_1_regwe),
    .set(decode_1_set), .shiftbyregval(decode_1_shiftbyregval), .setsign(decode_1_setsign),
    .AUIPC(decode_1_auipc), .ZeroOutA(decode_1_zeroouta), .MemHot(decode_1_memhot), .hasRs2(decode_1_hasrs2));
  // RegisterFile registerfile_1: pin names not known; wires that end beside it: registerfile_1_p1, not_1_out, registerfile_1_p3, registerfile_1_p4, decode_1_rs1, decode_1_rs2, registerfile_1_p7, registerfile_1_p8
  StallCtrl stallctrl_1 (
    .EX_MEM_MemHot(DE_EX_MemHot_q), .EX_MEM_rd(DE_EX_rd_q), .DE_EX_rs1(decode_1_rs1), .clock(clk),
    .DE_EX_rs2(decode_1_rs2), .hasRs2(decode_1_hasrs2), .stall(stallctrl_1_stall));
  not not_2 (not_2_out, stallctrl_1_stall);
  Register #(.width(32)) DE_EX_A (.D(registerfile_1_p7), .en(not_2_out), .clk(clk), .Q(DE_EX_A_q));  // open: clr
  Register #(.width(32)) DE_EX_B (.D(registerfile_1_p8), .en(not_2_out), .clk(clk), .Q(DE_EX_B_q));  // open: clr
  Register #(.width(5)) rs1 (.D(decode_1_rs1), .en(not_2_out), .clk(clk), .Q(rs1_q));  // open: clr
  Register #(.width(5)) rs2 (.D(decode_1_rs2), .en(not_2_out), .clk(clk), .Q(rs2_q));  // open: clr
  Register #(.width(5)) DE_EX_rd (.D(decode_1_rd), .en(not_2_out), .clk(clk), .Q(DE_EX_rd_q));  // open: clr
  Register #(.width(32)) DE_EX_imm (.D(decode_1_imm), .en(not_2_out), .clk(clk), .Q(DE_EX_imm_q));  // open: clr
  Register #(.width(1)) DE_EX_useImm (.D(decode_1_useimm), .en(not_2_out), .clk(clk), .Q(DE_EX_useImm_q));  // open: clr
  Register #(.width(4)) DE_EX_ALUop (.D(decode_1_aluop), .en(not_2_out), .clk(clk), .Q(DE_EX_ALUop_q));  // open: clr
  Register #(.width(32)) OneHot (.D(decode_1_onehot), .en(not_2_out), .clk(clk), .Q(OneHot_q));  // open: clr
  Register #(.width(1)) DE_EX_regWE (.D(decode_1_regwe), .en(not_2_out), .clk(clk), .Q(DE_EX_regWE_q));  // open: clr
  Register #(.width(1)) DE_EX_set (.D(decode_1_set), .en(not_2_out), .clk(clk), .Q(DE_EX_set_q));  // open: clr
  Register #(.width(1)) DE_EX_shiftreg (
    .D(decode_1_shiftbyregval), .en(not_2_out), .clk(clk), .Q(DE_EX_shiftreg_q));  // open: clr
  Register #(.width(1)) set_signed (.D(decode_1_setsign), .en(not_2_out), .clk(clk), .Q(set_signed_q));  // open: clr
  Register #(.width(32)) DE_EX_PC (.D(PC_q), .en(not_2_out), .clk(clk), .Q(DE_EX_PC_q));  // open: clr
  Register #(.width(1)) AUIPC (.D(decode_1_auipc), .en(not_2_out), .clk(clk), .Q(AUIPC_q));  // open: clr
  Register #(.width(1)) ZeroOutA (.D(decode_1_zeroouta), .en(not_2_out), .clk(clk), .Q(ZeroOutA_q));  // open: clr
  Register #(.width(4)) DE_EX_MemHot (.D(decode_1_memhot), .en(not_2_out), .clk(clk), .Q(DE_EX_MemHot_q));  // open: clr
  Register #(.width(32)) PCplus4ex (.D(PCplus4_q), .en(not_2_out), .clk(clk), .Q(PCplus4ex_q));  // open: clr
  // Bypass_Black_Box bypass_black_box_1: pin names not known; wires that end beside it: rs1_q, rs2_q, bypass_black_box_1_p3, bypass_black_box_1_p4, registerfile_1_p3, registerfile_1_p4, bypass_black_box_1_p7, bypass_black_box_1_p8
  nor nor_1 (nor_1_out, OneHot_q[26], OneHot_q[27], OneHot_q[28], OneHot_q[29], OneHot_q[30], OneHot_q[31]);
  or or_1 (or_1_out, OneHot_q[24], OneHot_q[25]);
  MUX3to1 mux3to1_1 (
    .out_5(mux3to1_1_out_5), .ME(EX_M_Result_q), .WB(registerfile_1_p1), .EX(DE_EX_B_q),
    .Sel(bypass_black_box_1_p8));
  or or_2 (or_2_out, AUIPC_q, OneHot_q[24]);
  and and_1 (and_1_out, DE_EX_useImm_q, nor_1_out);
  MUX3to1 mux3to1_2 (
    .out_5(mux3to1_2_out_5), .ME(EX_M_Result_q), .WB(registerfile_1_p1), .EX(DE_EX_A_q),
    .Sel(bypass_black_box_1_p7));
  Multiplexer #(.width(32), .enable("false")) multiplexer_4 (
    .in0(mux3to1_1_out_5), .in1(DE_EX_imm_q), .out(multiplexer_4_out), .sel(and_1_out));
  // Comparator_Black_Box comparator_black_box_1: pin names not known; wires that end beside it: mux3to1_2_out_5, multiplexer_4_out, set_signed_q, comparator_black_box_1_p4, comparator_black_box_1_p5, comparator_black_box_1_p6
  assign bit_extender_1_out = {{31{1'b0}}, comparator_black_box_1_p6};  // Bit_Extender bit_extender_1
  or or_3 (or_3_out, bctrl_1_branchctrl, or_1_out);
  Execute execute_1 (
    .A(mux3to1_2_out_5), .B(mux3to1_1_out_5), .rB(rs2_q), .imm(DE_EX_imm_q), .useImm(DE_EX_useImm_q),
    .ALUop(DE_EX_ALUop_q), .shiftbyregval(DE_EX_shiftreg_q), .UsePC(or_2_out), .PC(DE_EX_PC_q),
    .ZeroA(ZeroOutA_q), .result(execute_1_result));
  Bctrl bctrl_1 (
    .GT(comparator_black_box_1_p4), .EQ(comparator_black_box_1_p5), .LT(comparator_black_box_1_p6),
    .Branch(OneHot_q[31:26]), .branchctrl(bctrl_1_branchctrl));
  Multiplexer #(.width(32), .enable("false")) multiplexer_5 (
    .in0(execute_1_result), .in1(bit_extender_1_out), .out(multiplexer_5_out), .sel(DE_EX_set_q));
  Multiplexer #(.width(32), .enable("false")) multiplexer_6 (
    .in0(multiplexer_5_out), .in1(PCplus4ex_q), .out(multiplexer_6_out), .sel(or_1_out));
  assign and_2_out = mux3to1_1_out_5 & bit_extender_2_out;  // AND_Gate and_2, 32 bits wide
  assign bit_extender_2_out = {{31{not_2_out}}, not_2_out};  // Bit_Extender bit_extender_2
  assign bit_extender_3_out = {{4{not_2_out}}, not_2_out};  // Bit_Extender bit_extender_3
  assign bit_extender_4_out = {{3{not_2_out}}, not_2_out};  // Bit_Extender bit_extender_4
  Register #(.width(32)) EX_M_B (.D(and_2_out), .clk(clk), .Q(out_1));  // open: en, clr
  Register #(.width(32)) EX_M_Result (.D(and_3_out), .clk(clk), .Q(EX_M_Result_q));  // open: en, clr
  assign and_3_out = bit_extender_2_out & multiplexer_6_out;  // AND_Gate and_3, 32 bits wide
  Register #(.width(5)) EX_M_rd (.D(and_4_out), .clk(clk), .Q(bypass_black_box_1_p4));  // open: en, clr
  assign and_4_out = DE_EX_rd_q & bit_extender_3_out;  // AND_Gate and_4, 5 bits wide
  Register #(.width(1)) EX_M_regWE (.D(and_5_out), .clk(clk), .Q(bypass_black_box_1_p3));  // open: en, clr
  and and_5 (and_5_out, not_2_out, DE_EX_regWE_q);
  Register #(.width(4)) EX_M_MemHot (.D(and_6_out), .clk(clk), .Q(out_4));  // open: en, clr
  assign and_6_out = bit_extender_4_out & DE_EX_MemHot_q;  // AND_Gate and_6, 4 bits wide
  RAMCtrl ramctrl_1 (
    .Result(EX_M_Result_q), .Memhot(out_4), .EX_M_B(out_1), .sel(out_3), .lb_ctrl(ramctrl_1_lb_ctrl),
    .A(out_2), .ld(ramctrl_1_ld), .str(ramctrl_1_str), .B_Out(ramctrl_1_b_out));
  // RAM ram_1: pin names not known; wires that end beside it: out_2, ramctrl_1_b_out, ramctrl_1_str, out_3, clk, ramctrl_1_ld, ram_1_p7
  DataCtrl datactrl_1 (.Din(ram_1_p7), .lb_ctrl(ramctrl_1_lb_ctrl), .MemHot(out_4), .Dout(datactrl_1_dout));
  Register #(.width(1)) M_W_ld (.D(ramctrl_1_ld), .clk(clk), .Q(M_W_ld_q));  // open: en, clr
  Register #(.width(32)) M_W_Result (.D(EX_M_Result_q), .clk(clk), .Q(M_W_Result_q));  // open: en, clr
  Register #(.width(32)) M_W_Data (.D(datactrl_1_dout), .clk(clk), .Q(M_W_Data_q));  // open: en, clr
  Register #(.width(1)) M_W_regWE (.D(bypass_black_box_1_p3), .clk(clk), .Q(registerfile_1_p3));  // open: en, clr
  Register #(.width(5)) M_W_rd (.D(bypass_black_box_1_p4), .clk(clk), .Q(registerfile_1_p4));  // open: en, clr
  Multiplexer #(.width(32), .enable("false")) multiplexer_7 (
    .in0(M_W_Result_q), .in1(M_W_Data_q), .out(registerfile_1_p1), .sel(M_W_ld_q));

  // Notes on the sheet:
  //   Notes:
  //   not to force you into using a template
  //   This is a working circuit for all of the table A instructions
  //   - Feel free to change the structure of this for any reason
  //   as it is to save you from repeating work you've done,
  //   - Behavior for table B instructions is undefined in this release circuit
  //   - This should pass the sanity check if you submit it as is
  //   inverted stall signal
  //   contents of risc_vprogramrom_1 (hex, n*v repeats v):
  //   #expected behavior:  #x1: 000000005, x2: 000000009  #x3: 00000000e, x4: ffffffffb   addi x1, x0, 5
  //   addi x2, x1, 4 addi x0, x0, 4 add x3, x2, x1 sub x4, x2, x3  #testing addi, add, sub (table A) #x1:
  //   000000005, x2: 000000009  #x3: 00000000e, x4: ffffffffb   addi x1, x0, 5 addi x2, x1, 4 addi x0, x0,
  //   4 add x3, x2, x1 sub x4, x2, x3  #testing: and, andi, or, ori, xor, xori,  # slt, slti (Logic) in
  //   table A # Expected output:  # x1: 000000003, x2: 000000002, x3: 000000002, x4: 000000003, x5:
  //   000000001 # x6: 000000000, x7: 000000003, x8: 000000007, x9: 000000004, x10: 000000001 # x11:
  //   000000000, x12: 000000001  addi x1, x0, 3 addi x2, x0, 2 and x3, x1, x2 or x4, x1, x2 xor x5, x1, x2
  //   slt x6, x1, x2 andi x7, x1, 7 ori x8, x1, 7 xori x9, x1, 7 slti x10, x1, 4 sltu x11, x1, x2 sltiu
  //   x12, x1, 4  #testing: and, andi, or, ori, xor, xori,  # slt, slti (Logic) in table A # Expected
  //   output:  # x1: 000000003, x2: 000000002, x3: 000000002, x4: 000000003, x5: 000000001 # x6:
  //   000000000, x7: 000000003, x8: 000000007, x9: 000000004, x10: 000000001 # x11: 000000000, x12:
  //   000000001  addi x1, x0, 3 addi x2, x0, 2 and x3, x1, x2 or x4, x1, x2 xor x5, x1, x2 slt x6, x1, x2
  //   andi x7, x1, 7 ori x8, x1, 7 xori x9, x1, 7 slti x10, x1, 4 sltu x11, x1, x2 sltiu x12, x1, 4  #
  //   testing shifts: SRA, SRAI, SRL, SRLI, SLL, SLI (table A) # also: testing registers not used before,
  //   i.e. 20+ # x20: 1010, x21: 1111 # expected outputs: x20: 00000000a, x21: 00000000f, x22: 000000003,
  //   x23: 000000050, x24: 000000001  # x25: 000000a00, x26: 000000003, x27: 000000001  addi x20, x0, 10
  //   addi x21, x20, 5 addi x22, x0, 3 sll x23, x20, x22  srl x24, x21, x22 sra x25, x21, x22 slli x25,
  //   x20, 8 srli x26, x21, 2 srai x27, x21, 3     # testing shifts: SRA, SRAI, SRL, SRLI, SLL, SLI (table
  //   A) # also: testing registers not used before, i.e. 20+ # x20: 1010, x21: 1111 # expected outputs:
  //   x20: 00000000a, x21: 00000000f, x22: 000000003, x23: 000000050, x24: 000000001  # x25: 000000a00,
  //   x26: 000000003, x27: 000000001  addi x20, x0, 10 addi x21, x20, 5 addi x22, x0, 3 sll x23, x20, x22
  //   srl x24, x21, x22 sra x25, x21, x22 slli x25, x20, 8 srli x26, x21, 2 srai x27, x21, 3   #auipc +
  //   lui test #expected outputs:  #x1: 000008000, x2: 000001000, x3: 000008008, x4: 00000800c  lui x1, 8
  //   lui x2, 1 auipc x3, 8 auipc x4, 8   #testing sw, lw, lb #expected behavior: #In register file: #x1:
  //   12345678, x2: abcde123 #x3: 4       , x4: 12345678 #x5: abcde123, #x6: 23, x7: e1, x8: cd, x9: ab
  //   #In RAM: #Word 0: 12345678 #Word 2: abcde123  LUI x1, 0x12345 ADDI x1, x1, 0x678 LUI x2, 0xabcde
  //   ADDI x2, x2, 0x123 ADDI x3, x3, 4  SW x1, 0(x0) SW x2, 4(x3)  LW x4, 0(x0) LW x5, 4(x3)  LB x6,
  //   4(x3) LB x7, 5(x3) LB x8, 6(x3) LB x9, 7(x3)  #testing sb #expected behavior: #x11: a1b2c3d4 #x12:
  //   000000d4 #x13: 0000d400 #x14: 00d40000 #x15: d4000000  LUI x11, 0xa1b2c ADDI x11, x11, 0x3d4 ADDI
  //   x16, x0, 16  SB x11, 0(x16) lw x12, 0(x16) SB x11, 5(x16) lw x13, 4(x16) SB x11, 10(x16) lw x14,
  //   8(x16) SB x11, 15(x16) lw x15, 12(x16)  #hazard detection tests: #expected behavior: #x1: 2, x2: 3,
  //   x3: 5 #x4: 7, x5: 6, x6: d #x7: 3, x8: f, x9: 5 #x10: 7  #forward from MW to A, forward from XM to B
  //   ADDI x1, x0, 2 ADDI x2, x0, 3 ADD x3, x1, x2  #forward from XM to A, forward from MW to B ADDI x4,
  //   x0, 7 ADDI x5, x0, 6 ADD x6, x5, x4  #data hazard detection SW x2, 0(x0) LW x7, 0(x0) #should stall
  //   so x7 can update ADDI x8, x7, 12 SW x3, 4(x0) LW x9, 4(x0) #should stall so x9 can update ADD x10,
  //   x9, x1  #testing jal #expected behavior: #x18: 00000174 #x19: 00000000 #x20: 0000017c #x21: 00000005
  //   JAL x18, 8 ADDI x19, x0, 10 JAL x20, 4 ADDI x21, x0, 5  #testing jalr #expected behavior: #x22:
  //   00000184 #x19: 00000000 #x25: 00000017 #x23: 00000190 #x26: 00000005   JALR x22, x18, 20 ADDI x19,
  //   x0, 10 ADDI x25, x0, 23 JALR x23, x20, 20  ADDI x26, x0, 5  #testing BEQ #expected behavior: #x26:
  //   00000001 #x27: 00000000 #x28: 00000002 #x29: 00000002 #x30: 00000001 #x31: 00000001   ADDI x27, x0,
  //   0 ADDI x28, x0, 2 ADDI x29, x0, 2 BEQ  x28, x29, 8 ADDI x27, x0,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
  //   go for it!
  //   and execute is for readability. If you
  //   The amount of registers between decode
  //   do want to combine them into less registers,
  //   Register Write Enable
endmodule

module Fetching (
  input  clk,
  output [31:0] intr
);

  wire [31:0] increment_pc_1_out_2, register_1_q;

  Register #(.width(32), .trigger("falling")) register_1 (
    .D(increment_pc_1_out_2), .clk(clk), .Q(register_1_q));  // open: en, clr
  Increment_PC increment_pc_1 (.in_1(register_1_q), .out_2(increment_pc_1_out_2));
endmodule

module Increment_PC (
  input  [31:0] in_1,
  output [31:0] out_2
);

  // Incrementer #(.width(30)) incrementer_1: pin names not known; wires that end beside it: in_1[31:2], out_2[31:2]

  assign out_2[1:0] = in_1[1:0];
endmodule

module Decode (
  input  [31:0] instr,
  output [4:0] rs1,
  output [4:0] rs2,
  output [4:0] rd,
  output [31:0] imm,
  output useImm,
  output [3:0] ALUop,
  output [31:0] onehot,
  output regWE,
  output set,
  output shiftbyregval,
  output setsign,
  output AUIPC,
  output ZeroOutA,
  output [3:0] MemHot,
  output hasRs2
);

  wire decode_black_box_1_p6, or_1_out, or_2_out, or_3_out, or_6_out, or_8_out, or_10_out;
  wire [3:0] decode_black_box_1_p7;
  wire [3:3] or_11_out;
  wire [11:0] multiplexer_1_out;
  wire [31:0] bit_extender_1_out, branchimm_1_out_2, decode_black_box_1_p5, jalimm_1_jumpimm,
       multiplexer_2_out, multiplexer_3_out;

  // Decode_Black_Box decode_black_box_1: pin names not known; wires that end beside it: instr, rs1, rs2, rd, decode_black_box_1_p5, decode_black_box_1_p6, decode_black_box_1_p7, onehot[0], onehot[1], onehot[2], onehot[3], onehot[4], onehot[5], onehot[6], onehot[7], onehot[8], onehot[9], onehot[10], onehot[11], onehot[12], onehot[13], onehot[14], onehot[15], onehot[16], onehot[17], onehot[18], onehot[19], onehot[20], onehot[21], MemHot[0], MemHot[1], onehot[24], onehot[25], onehot[26], onehot[27], onehot[28], onehot[29], onehot[30]
  or or_1 (or_1_out, instr[4], ~instr[5]);  // OR_Gate
  or or_2 (or_2_out, onehot[19], onehot[17], onehot[15], MemHot[2], MemHot[0], onehot[13], onehot[11], onehot[9], onehot[7], onehot[5], onehot[1], onehot[24], onehot[25]);
  not not_1 (hasRs2, or_2_out);
  or or_3 (or_3_out, MemHot[3], MemHot[1]);
  or or_4 (set, onehot[13], onehot[12], onehot[11], onehot[10]);
  or or_5 (shiftbyregval, onehot[14], onehot[16], onehot[18]);
  Multiplexer #(.width(12), .enable("false")) multiplexer_1 (
    .in0(instr[31:20]), .in1({instr[31:25], instr[11:7]}), .out(multiplexer_1_out), .sel(or_3_out));
  or or_6 (or_6_out, onehot[26], onehot[27], onehot[28], onehot[29], onehot[30], onehot[31]);
  or or_7 (setsign, onehot[11], onehot[10], onehot[26], onehot[27], onehot[28], onehot[29]);
  assign bit_extender_1_out = {{20{multiplexer_1_out[11]}}, multiplexer_1_out};  // Bit_Extender bit_extender_1
  JALimm jalimm_1 (.imm(decode_black_box_1_p5), .Jalctrl(onehot[24]), .Jumpimm(jalimm_1_jumpimm));
  or or_8 (or_8_out, onehot[24], onehot[25]);
  Multiplexer #(.width(32), .enable("false")) multiplexer_2 (
    .in0(decode_black_box_1_p5), .in1(jalimm_1_jumpimm), .out(multiplexer_2_out), .sel(or_8_out));
  or or_9 (AUIPC, onehot[24], or_6_out, onehot[21]);
  or or_10 (or_10_out, MemHot[0], MemHot[1], MemHot[2], MemHot[3]);
  or or_11 (or_11_out[3], decode_black_box_1_p7[3], or_8_out, or_6_out);
  or or_12 (regWE, or_8_out, or_1_out);
  Multiplexer #(.width(32), .enable("false")) multiplexer_3 (
    .in0(multiplexer_2_out), .in1(branchimm_1_out_2), .out(multiplexer_3_out), .sel(or_6_out));
  Branchimm branchimm_1 (.in_1(multiplexer_2_out), .out_2(branchimm_1_out_2));
  Multiplexer #(.width(32), .enable("false")) multiplexer_4 (
    .in0(multiplexer_3_out), .in1(bit_extender_1_out), .out(imm), .sel(or_10_out));
  Multiplexer #(.width(4), .enable("false")) multiplexer_5 (
    .in0({or_11_out[3], decode_black_box_1_p7[2:0]}), .in1(4'b1000), .out(ALUop), .sel(or_10_out));
  or or_13 (useImm, decode_black_box_1_p6, or_10_out);

  assign onehot[23:22] = MemHot[1:0];
  assign ZeroOutA = onehot[20];

  // Notes on the sheet:
  //   1 if op is LW, SW, LB, or SB
  //   Feel free to output the 1 hot if you want!
  //   Example of different ways to decode using what's given
endmodule

module Execute (
  input  [31:0] A,
  input  [31:0] B,
  input  [4:0] rB,
  input  [31:0] imm,
  input  useImm,
  input  [3:0] ALUop,
  input  shiftbyregval,
  input  UsePC,
  input  [31:0] PC,
  input  ZeroA,
  output [31:0] result
);

  wire not_1_out;
  wire [4:0] multiplexer_3_out;
  wire [31:0] and_1_out, bit_extender_1_out, multiplexer_1_out, multiplexer_2_out, multiplexer_4_out;

  not not_1 (not_1_out, ZeroA);
  assign bit_extender_1_out = {{31{not_1_out}}, not_1_out};  // Bit_Extender bit_extender_1
  Multiplexer #(.width(32), .enable("false")) multiplexer_1 (.in0(B), .in1(imm), .out(multiplexer_1_out), .sel(useImm));
  Multiplexer #(.width(32), .enable("false")) multiplexer_2 (
    .in0(multiplexer_1_out), .in1(A), .out(multiplexer_2_out), .sel(shiftbyregval));
  Multiplexer #(.width(5), .enable("false")) multiplexer_3 (
    .in0(rB), .in1(B[4:0]), .out(multiplexer_3_out), .sel(shiftbyregval));
  Multiplexer #(.width(32), .enable("false")) multiplexer_4 (.in0(A), .in1(PC), .out(multiplexer_4_out), .sel(UsePC));
  assign and_1_out = multiplexer_4_out & bit_extender_1_out;  // AND_Gate and_1, 32 bits wide
  // ALU alu_1: pin names not known; wires that end beside it: and_1_out, multiplexer_2_out, ALUop, multiplexer_3_out, result
endmodule

module MUX3to1 (
  input  [1:0] Sel,
  input  [31:0] EX,
  input  [31:0] WB,
  input  [31:0] ME,
  output [31:0] out_5
);

  wire [31:0] multiplexer_1_out;

  Multiplexer #(.width(32), .enable("false")) multiplexer_1 (.in0(EX), .in1(WB), .out(multiplexer_1_out), .sel(Sel[0]));
  Multiplexer #(.width(32), .enable("false")) multiplexer_2 (
    .in0(multiplexer_1_out), .in1(ME), .out(out_5), .sel(Sel[1]));
endmodule

module JALimm (
  input  [31:0] imm,
  input  Jalctrl,
  output [31:0] Jumpimm
);

  wire [0:0] not_1_out;
  wire [30:0] bit_extender_2_out;
  wire [31:0] bit_extender_1_out;

  assign bit_extender_1_out = {{20{imm[11]}}, {imm[11:1], Jalctrl}};  // Bit_Extender bit_extender_1
  assign bit_extender_2_out = {{11{imm[31]}}, {imm[31], imm[19:12], imm[20], imm[30:21]}};  // Bit_Extender bit_extender_2
  not not_1 (not_1_out[0], Jalctrl);
  Multiplexer #(.width(32), .enable("false")) multiplexer_1 (
    .in0(bit_extender_1_out), .in1({bit_extender_2_out, not_1_out[0]}), .out(Jumpimm), .sel(Jalctrl));
endmodule

module ZapInst (
  input  Zap,
  output [31:0] Nopinst
);

  wire [3:2] not_1_out;

  not not_1 (not_1_out[2], Zap);
  not not_2 (not_1_out[3], Zap);
  assign Nopinst = {{27{1'b0}}, {Zap, not_1_out, {2{Zap}}}};  // Bit_Extender bit_extender_1
endmodule

module Bctrl (
  input  GT,
  input  EQ,
  input  LT,
  input  [5:0] Branch,
  output branchctrl
);

  wire and_1_out, and_2_out, and_3_out, and_4_out, or_1_out, or_2_out, or_3_out, or_4_out;

  or or_1 (or_1_out, Branch[2], Branch[4]);
  or or_2 (or_2_out, GT, LT);
  and and_1 (and_1_out, LT, or_1_out);
  and and_2 (and_2_out, or_2_out, Branch[1]);
  and and_3 (and_3_out, EQ, Branch[0]);
  or or_3 (or_3_out, GT, EQ);
  or or_4 (or_4_out, Branch[3], Branch[5]);
  and and_4 (and_4_out, or_3_out, or_4_out);
  or or_5 (branchctrl, and_2_out, and_3_out, and_1_out, and_4_out);
endmodule

module Branchimm (
  input  [31:0] in_1,
  output [31:0] out_2
);

  assign out_2 = {{19{in_1[12]}}, in_1[12:0]};  // Bit_Extender bit_extender_1
endmodule

module RAMCtrl (
  input  [31:0] Result,
  input  [3:0] Memhot,
  input  [31:0] EX_M_B,
  output [3:0] sel,
  output [1:0] lb_ctrl,
  output [19:0] A,
  output ld,
  output str,
  output [31:0] B_Out
);

  wire or_3_out;
  wire [3:0] and_4_out, bit_extender_1_out;

  Multiplexer #(.width(32), .enable("false")) multiplexer_1 (
    .in0(EX_M_B), .in1({EX_M_B[7:0], EX_M_B[7:0], EX_M_B[7:0], EX_M_B[7:0]}), .out(B_Out), .sel(Memhot[3]));
  or or_1 (ld, Memhot[0], Memhot[2]);
  or or_2 (str, Memhot[1], Memhot[3]);
  or or_3 (or_3_out, Memhot[0], Memhot[1]);
  and and_1 (and_4_out[3], Result[1], Result[0]);
  and and_2 (and_4_out[2], Result[1], ~Result[0]);  // AND_Gate
  and and_3 (and_4_out[1], ~Result[1], Result[0]);  // AND_Gate
  and and_4 (and_4_out[0], ~Result[1], ~Result[0]);  // AND_Gate
  assign bit_extender_1_out = {{3{or_3_out}}, or_3_out};  // Bit_Extender bit_extender_1
  assign sel = and_4_out | bit_extender_1_out;  // OR_Gate or_4, 4 bits wide

  assign A = Result[21:2];
  assign lb_ctrl = Result[1:0];

  // Notes on the sheet:
  //   Bit 0: lw 
  //   Bit 1: sw
  //   Bit 2: lb
  //   Bit 3: sb
  //   One hot encoding of memory ops:
  //   byte address
endmodule

module DataCtrl (
  input  [31:0] Din,
  input  [1:0] lb_ctrl,
  input  [3:0] MemHot,
  output [31:0] Dout
);

  wire [7:0] multiplexer_1_out;
  wire [31:0] bit_extender_1_out;

  Multiplexer #(.select(2), .width(8), .enable("false")) multiplexer_1 (
    .in0(Din[7:0]), .in1(Din[15:8]), .in2(Din[23:16]), .in3(Din[31:24]), .out(multiplexer_1_out),
    .sel(lb_ctrl));
  assign bit_extender_1_out = {{24{1'b0}}, multiplexer_1_out};  // Bit_Extender bit_extender_1
  Multiplexer #(.width(32), .enable("false")) multiplexer_2 (
    .in0(Din), .in1(bit_extender_1_out), .out(Dout), .sel(MemHot[2]));

  // Notes on the sheet:
  //   1 if lb, 0 otherwise
endmodule

module StallCtrl (
  input  [3:0] EX_MEM_MemHot,
  input  [4:0] EX_MEM_rd,
  input  [4:0] DE_EX_rs1,
  input  clock,
  input  [4:0] DE_EX_rs2,
  input  hasRs2,
  output stall
);

  wire and_1_out, and_2_out, and_3_out, and_4_out, or_1_out, or_2_out, or_3_out;
  wire [4:0] xnor_1_out, xnor_2_out;

  or or_1 (or_1_out, EX_MEM_MemHot[0], EX_MEM_MemHot[2]);
  or or_2 (or_2_out, EX_MEM_rd[0], EX_MEM_rd[1], EX_MEM_rd[2], EX_MEM_rd[3], EX_MEM_rd[4]);
  assign xnor_1_out = ~(DE_EX_rs1 ^ EX_MEM_rd);  // XNOR_Gate xnor_1, 5 bits wide
  assign xnor_2_out = ~(EX_MEM_rd ^ DE_EX_rs2);  // XNOR_Gate xnor_2, 5 bits wide
  and and_1 (and_1_out, xnor_1_out[0], xnor_1_out[1], xnor_1_out[2], xnor_1_out[3], xnor_1_out[4]);
  and and_2 (and_2_out, xnor_2_out[0], xnor_2_out[1], xnor_2_out[2], xnor_2_out[3], xnor_2_out[4]);
  and and_3 (and_3_out, and_2_out, hasRs2);
  or or_3 (or_3_out, and_1_out, and_3_out);
  Register #(.width(1)) register_1 (.D(and_4_out), .clk(clock), .Q(stall));  // open: en, clr
  and and_4 (and_4_out, or_1_out, or_2_out, or_3_out);

  // Notes on the sheet:
  //   Bit 0: lw 
  //   Bit 1: sw
  //   Bit 2: lb
  //   Bit 3: sb
endmodule
