// Logisim project RISCV.circ as structural Verilog: 9 circuits, main circuit main
module main (
);

  wire Clk_out, decode_1_p2, decode_1_p5, decode_1_p6, RType_q;
  wire [2:0] decode_1_p4;
  wire [3:0] ALUOp_q, getaluop_1_aluop;
  wire [4:0] decode_1_p3, IXRd_q, registerfile_1_p3, XMRd_q;
  wire [6:0] decode_1_p8;
  wire [31:0] alu_1_p5, decode_1_p7, fetch_1_instr, fetch_1_pcplus4, Imm_q, Instr_q, IXA_q, IXB_q,
       multiplexer_1_out, registerfile_1_p1, registerfile_1_p6, registerfile_1_p7, XMD_q;

  Clock Clk (.out(Clk_out));
  Fetch fetch_1 (.Clk(Clk_out), .Instr(fetch_1_instr), .PCPlus4(fetch_1_pcplus4));
  Register #(.width(32)) Instr (.D(fetch_1_instr), .clk(Clk_out), .Q(Instr_q));  // open: en, clr
  Register #(.width(32)) PCPlus4 (.D(fetch_1_pcplus4), .clk(Clk_out));  // open: en, Q, clr
  // Decode decode_1: pin names not known; wires that end beside it: Instr_q, decode_1_p2, decode_1_p3, decode_1_p4, decode_1_p5, decode_1_p6, decode_1_p7, decode_1_p8
  // RegisterFile registerfile_1: pin names not known; wires that end beside it: registerfile_1_p1, Clk_out, registerfile_1_p3, decode_1_p5, decode_1_p6, registerfile_1_p6, registerfile_1_p7
  Register #(.width(32)) IXA (.D(registerfile_1_p6), .clk(Clk_out), .Q(IXA_q));  // open: en, clr
  Register #(.width(32)) IXB (.D(registerfile_1_p7), .clk(Clk_out), .Q(IXB_q));  // open: en, clr
  Register #(.width(32)) Imm (.D(decode_1_p7), .clk(Clk_out), .Q(Imm_q));  // open: en, clr
  Register #(.width(4)) ALUOp (.D(getaluop_1_aluop), .clk(Clk_out), .Q(ALUOp_q));  // open: en, clr
  GetALUOp getaluop_1 (.IsR(decode_1_p2), .Funct7(decode_1_p8), .Funct3(decode_1_p4), .ALUOp(getaluop_1_aluop));
  Register #(.width(1)) RType (.D(decode_1_p2), .clk(Clk_out), .Q(RType_q));  // open: en, clr
  Register #(.width(5)) IXRd (.D(decode_1_p3), .clk(Clk_out), .Q(IXRd_q));  // open: en, clr
  Multiplexer #(.width(32), .enable("false")) multiplexer_1 (
    .in0(Imm_q), .in1(IXB_q), .out(multiplexer_1_out), .sel(RType_q));
  // ALU alu_1: pin names not known; wires that end beside it: IXA_q, multiplexer_1_out, ALUOp_q, IXB_q[4:0], alu_1_p5
  Comparator comparator_1 ();  // open: a, b, gt, eq, lt
  Register #(.width(32)) XMD (.D(alu_1_p5), .clk(Clk_out), .Q(XMD_q));  // open: en, clr
  Register #(.width(32)) XMB (.D(IXB_q), .clk(Clk_out));  // open: en, Q, clr
  Register #(.width(5)) XMRd (.D(IXRd_q), .clk(Clk_out), .Q(XMRd_q));  // open: en, clr
  Register #(.width(32)) MWD (.D(XMD_q), .clk(Clk_out), .Q(registerfile_1_p1));  // open: en, clr
  Register #(.width(5)) MWRd (.D(XMRd_q), .clk(Clk_out), .Q(registerfile_1_p3));  // open: en, clr
endmodule

module Fetch (
  input  Clk,
  output [31:0] Instr,
  output [31:0] PCPlus4
);

  wire [29:0] register_1_q;

  Register #(.width(32)) register_1 (.D(PCPlus4), .clk(Clk), .Q({register_1_q, PCPlus4[1:0]}));  // open: en, clr
  // Incrementer #(.width(30)) incrementer_1: pin names not known; wires that end beside it: Clk, register_1_q, PCPlus4[31:2], {register_1_q, PCPlus4[1:0]}
  // RISC_VProgramROM risc_vprogramrom_1: pin names not known; wires that end beside it: Instr

  // Notes on the sheet:
  //   contents of risc_vprogramrom_1 (hex, n*v repeats v):
  //   auipc x3,1
endmodule

module DecodeOld (
  input  [31:0] w,
  input  WE,
  input  [31:0] xW,
  input  [31:0] inst,
  input  [31:0] PCplus4,
  output [31:0] xA,
  output [31:0] xB,
  output [15:0] control,
  output [31:0] imm
);

  wire [4:0] instdecode_1_xa, instdecode_1_xb;

  instdecode instdecode_1 (
    .inst(inst), .PCplus4(PCplus4), .xA(instdecode_1_xa), .xB(instdecode_1_xb), .control(control), .imm(imm));
  // RegisterFile registerfile_1: pin names not known; wires that end beside it: w, WE, xW, instdecode_1_xa, instdecode_1_xb, xA, xB
endmodule

module instdecode (
  input  [31:0] inst,
  input  [31:0] PCplus4,
  output [4:0] xA,
  output [4:0] xB,
  output [15:0] control,
  output [31:0] imm
);

  wire not_1_out;
  wire [31:0] adder_1_out, bit_extender_1_out, bit_extender_2_out, multiplexer_1_out;

  decodetoop decodetoop_1 (.Funct3(inst[14:12]), .ALUinst(control[15:12]));  // open: Funct7Snd
  assign bit_extender_1_out = {{12{1'b0}}, {inst[12], inst[13], inst[14], inst[15], inst[16], inst[17], inst[18], inst[19], inst[20], inst[21], inst[22], inst[23], inst[24], inst[25], inst[26], inst[27], inst[28], inst[29], inst[30], inst[31]}};  // Bit_Extender bit_extender_1
  assign bit_extender_2_out = {{20{inst[31]}}, inst[31:20]};  // Bit_Extender bit_extender_2
  Adder #(.width(32)) adder_1 (
    .a({bit_extender_1_out[0], bit_extender_1_out[1], bit_extender_1_out[2], bit_extender_1_out[3], bit_extender_1_out[4], bit_extender_1_out[5], bit_extender_1_out[6], bit_extender_1_out[7], bit_extender_1_out[8], bit_extender_1_out[9], bit_extender_1_out[10], bit_extender_1_out[11], bit_extender_1_out[12], bit_extender_1_out[13], bit_extender_1_out[14], bit_extender_1_out[15], bit_extender_1_out[16], bit_extender_1_out[17], bit_extender_1_out[18], bit_extender_1_out[19], bit_extender_1_out[20], bit_extender_1_out[21], bit_extender_1_out[22], bit_extender_1_out[23], bit_extender_1_out[24], bit_extender_1_out[25], bit_extender_1_out[26], bit_extender_1_out[27], bit_extender_1_out[28], bit_extender_1_out[29], bit_extender_1_out[30], bit_extender_1_out[31]}),
    .b(PCplus4), .out(adder_1_out));  // open: cin, cout
  Multiplexer #(.width(32), .enable("false")) multiplexer_1 (
    .in0(adder_1_out),
    .in1({bit_extender_1_out[0], bit_extender_1_out[1], bit_extender_1_out[2], bit_extender_1_out[3], bit_extender_1_out[4], bit_extender_1_out[5], bit_extender_1_out[6], bit_extender_1_out[7], bit_extender_1_out[8], bit_extender_1_out[9], bit_extender_1_out[10], bit_extender_1_out[11], bit_extender_1_out[12], bit_extender_1_out[13], bit_extender_1_out[14], bit_extender_1_out[15], bit_extender_1_out[16], bit_extender_1_out[17], bit_extender_1_out[18], bit_extender_1_out[19], bit_extender_1_out[20], bit_extender_1_out[21], bit_extender_1_out[22], bit_extender_1_out[23], bit_extender_1_out[24], bit_extender_1_out[25], bit_extender_1_out[26], bit_extender_1_out[27], bit_extender_1_out[28], bit_extender_1_out[29], bit_extender_1_out[30], bit_extender_1_out[31]}),
    .out(multiplexer_1_out), .sel(inst[5]));
  not not_1 (not_1_out, inst[2]);
  Multiplexer #(.width(32), .enable("false")) multiplexer_2 (
    .in0(multiplexer_1_out), .in1(bit_extender_2_out), .out(imm), .sel(not_1_out));

  assign control[11:0] = inst[11:0];
  assign xA = inst[19:15];
  assign xB = inst[24:20];
endmodule

module decodetoop (
  input  [2:0] Funct3,
  input  Funct7Snd,
  output [3:0] ALUinst
);

  wire and_1_out, and_2_out, nand_1_out, nor_1_out, nor_2_out, not_1_out, not_2_out, not_3_out, not_4_out,
       or_4_out, xor_1_out;

  and and_1 (and_1_out, Funct7Snd, Funct3[0], not_1_out);
  not not_1 (not_1_out, Funct3[1]);
  not not_2 (not_2_out, Funct3[2]);
  or or_1 (ALUinst[0], and_1_out, not_2_out);
  not not_3 (not_3_out, Funct3[0]);
  and and_2 (and_2_out, not_3_out, Funct3[2]);
  xor xor_1 (xor_1_out, Funct3[1], Funct3[2]);
  nor nor_1 (nor_1_out, Funct3[0], Funct3[1], Funct3[2], not_4_out);
  not not_4 (not_4_out, Funct7Snd);
  or or_2 (ALUinst[3], and_2_out, Funct3[1]);
  nor nor_2 (nor_2_out, Funct3[2], Funct3[0]);
  nand nand_1 (nand_1_out, Funct3[0], Funct3[2]);
  or or_3 (ALUinst[2], xor_1_out, nor_1_out);
  or or_4 (or_4_out, Funct3[1], nor_2_out);
  and and_3 (ALUinst[1], or_4_out, nand_1_out);
endmodule

module Decode (
  input  [31:0] Instr,
  input  [31:0] pcplus4,
  output RType,
  output [6:0] Op7,
  output [4:0] Rd5,
  output [2:0] Funct3,
  output [4:0] Rs1,
  output [31:0] out_8,
  output [4:0] Rs2,
  output [31:0] Imm,
  output [6:0] Funct7
);

  wire and_1_out, not_1_out, optotype_1_b, optotype_1_ifunc, optotype_1_inon, optotype_1_j, optotype_1_s,
       optotype_1_u, or_1_out;
  wire [6:0] bit_extender_1_out;
  wire [11:0] multiplexer_2_out;
  wire [31:0] adder_1_out, bit_extender_3_out, multiplexer_3_out;

  OpToType optotype_1 (
    .Op6(Instr[6]), .Op5(Instr[5]), .Op4(Instr[4]), .Op3(Instr[3]), .Op2(Instr[2]), .R(RType),
    .U(optotype_1_u), .IFunc(optotype_1_ifunc), .INon(optotype_1_inon), .J(optotype_1_j), .S(optotype_1_s),
    .B(optotype_1_b));
  or or_1 (or_1_out, optotype_1_inon, optotype_1_j, optotype_1_s, optotype_1_b);
  assign bit_extender_1_out = {{6{or_1_out}}, or_1_out};  // Bit_Extender bit_extender_1
  Multiplexer #(.width(7), .enable("false")) multiplexer_1 (
    .in0(Instr[6:0]), .in1(bit_extender_1_out), .out(Op7), .sel(or_1_out));
  assign out_8 = {{12{Instr[31]}}, Instr[31:12]};  // Bit_Extender bit_extender_2
  Multiplexer #(.width(12), .enable("false")) multiplexer_2 (
    .in0({Instr[31:25], Instr[11:7]}), .in1(Instr[31:20]), .out(multiplexer_2_out), .sel(optotype_1_ifunc));
  assign bit_extender_3_out = {{20{multiplexer_2_out[11]}}, multiplexer_2_out};  // Bit_Extender bit_extender_3
  Multiplexer #(.width(32), .enable("false")) multiplexer_3 (
    .in0(bit_extender_3_out), .in1(out_8), .out(multiplexer_3_out), .sel(optotype_1_u));
  Adder #(.width(32)) adder_1 (.a(multiplexer_3_out), .b(pcplus4), .out(adder_1_out));  // open: cin, cout
  and and_1 (and_1_out, Instr[2], not_1_out);
  not not_1 (not_1_out, Instr[5]);
  Multiplexer #(.width(32), .enable("false")) multiplexer_4 (
    .in0(multiplexer_3_out), .in1(adder_1_out), .out(Imm), .sel(and_1_out));

  assign Funct3 = Instr[14:12];
  assign Funct7 = Instr[31:25];
  assign Rd5 = Instr[11:7];
  assign Rs1 = Instr[19:15];
  assign Rs2 = Instr[24:20];

  // Notes on the sheet:
  //   Funct7
  //   Imm7
  //   Rs1
  //   Rs2
  //   Op7
  //   Rd5
  //   Imm5
  //   Funct3
  //   U-type
  //   I-type
  //   S-type
endmodule

module OpToType (
  input  Op6,
  input  Op5,
  input  Op4,
  input  Op3,
  input  Op2,
  output R,
  output U,
  output IFunc,
  output INon,
  output J,
  output S,
  output B
);

  wire and_1_out, and_2_out, and_5_out, and_6_out, not_1_out, not_2_out, not_3_out, not_4_out, not_5_out,
       not_6_out, not_7_out, not_8_out, not_9_out, not_10_out, not_11_out, not_12_out, not_13_out;

  not not_1 (not_1_out, Op6);
  not not_2 (not_2_out, Op4);
  not not_3 (not_3_out, Op2);
  not not_4 (not_4_out, Op6);
  not not_5 (not_5_out, Op5);
  not not_6 (not_6_out, Op2);
  not not_7 (not_7_out, Op5);
  not not_8 (not_8_out, Op4);
  not not_9 (not_9_out, Op3);
  not not_10 (not_10_out, Op6);
  not not_11 (not_11_out, Op4);
  not not_12 (not_12_out, Op2);
  not not_13 (not_13_out, Op2);
  and and_1 (and_1_out, not_1_out, not_2_out, Op2);
  and and_2 (and_2_out, Op5, Op4, not_3_out);
  and and_3 (U, not_4_out, Op2);
  and and_4 (IFunc, not_5_out, Op4, not_6_out);
  and and_5 (and_5_out, not_7_out, not_8_out);
  and and_6 (and_6_out, Op6, not_9_out, Op2);
  and and_7 (S, not_10_out, Op5, not_11_out, not_12_out);
  and and_8 (B, Op6, not_13_out);
  or or_1 (R, and_1_out, and_2_out);
  or or_2 (INon, and_5_out, and_6_out);

  assign J = Op3;
endmodule

module GetALUOpSub (
  input  IsR,
  input  F5,
  input  Funct2,
  input  Funct1,
  input  Funct0,
  output Op3,
  output Op2,
  output Op1,
  output Op0
);

  wire and_1_out, and_2_out, and_3_out, and_4_out, not_1_out, not_2_out, not_3_out, not_4_out, not_5_out;

  not not_1 (not_1_out, Funct1);
  not not_2 (not_2_out, Funct1);
  not not_3 (not_3_out, Funct1);
  not not_4 (not_4_out, Funct0);
  not not_5 (not_5_out, Funct2);
  and and_1 (and_1_out, not_1_out, Funct0);
  and and_2 (and_2_out, Funct2, not_2_out);
  and and_3 (and_3_out, IsR, F5);
  and and_4 (and_4_out, Funct2, not_3_out);
  or or_1 (Op0, not_4_out, Funct1, F5);
  or or_2 (Op3, not_5_out, and_1_out);
  or or_3 (Op2, and_2_out, and_3_out);
  or or_4 (Op1, Funct0, and_4_out);
endmodule

module GetALUOp (
  input  IsR,
  input  [6:0] Funct7,
  input  [2:0] Funct3,
  output [3:0] ALUOp
);

  GetALUOpSub getaluopsub_1 (
    .IsR(IsR), .F5(Funct7[5]), .Funct2(Funct3[0]), .Funct1(Funct3[1]), .Funct0(Funct3[2]), .Op3(ALUOp[3]),
    .Op2(ALUOp[2]), .Op1(ALUOp[1]), .Op0(ALUOp[0]));
endmodule
