// Logisim project RISCV.circ as structural Verilog: 8 circuits, main circuit RISCV32
module RISCV32 (
);

  wire AUIPC_q, bypass_black_box_1_p3, clk, comparator_black_box_1_p4, DE_EX_regWE_q, DE_EX_set_q,
       DE_EX_shiftreg_q, DE_EX_useImm_q, decode_1_auipc, decode_1_regwe, decode_1_set, decode_1_setsign,
       decode_1_shiftbyregval, decode_1_useimm, decode_1_zeroouta, not_1_out, or_1_out, or_2_out,
       registerfile_1_p3, set_signed_q, ZeroOutA_q;
  wire [1:0] bypass_black_box_1_p7, bypass_black_box_1_p8;
  wire [3:0] DE_EX_ALUop_q, decode_1_aluop;
  wire [4:0] bypass_black_box_1_p4, DE_EX_rd_q, decode_1_rd, decode_1_rs1, decode_1_rs2, registerfile_1_p4,
       rs1_q, rs2_q;
  wire [31:0] bit_extender_1_out, DE_EX_A_q, DE_EX_B_q, DE_EX_imm_q, DE_EX_PC_q, decode_1_imm,
       decode_1_onehot, EX_M_Result_q, execute_1_result, IF_DE_instr_q, increment_pc_1_out_2,
       multiplexer_1_out, multiplexer_2_out, multiplexer_3_out, multiplexer_4_out, multiplexer_5_out,
       multiplexer_6_out, mux3to1_1_out_5, mux3to1_2_out_5, OneHot_q, PC_q, register_1_q, registerfile_1_p1,
       registerfile_1_p7, registerfile_1_p8, risc_vprogramrom_1_p2, zapinst_1_nopinst;

  Clock clock_1 (.out(clk));
  Register #(.width(32)) register_1 (.D(multiplexer_1_out), .clk(clk), .Q(register_1_q));  // open: en, clr
  Multiplexer #(.width(32), .enable("false")) multiplexer_1 (
    .in0(increment_pc_1_out_2), .in1(execute_1_result), .out(multiplexer_1_out), .sel(or_1_out));
  Increment_PC increment_pc_1 (.in_1(register_1_q), .out_2(increment_pc_1_out_2));
  Register #(.width(32)) IF_DE_instr (.D(multiplexer_2_out), .clk(clk), .Q(IF_DE_instr_q));  // open: en, clr
  // RISC_VProgramROM risc_vprogramrom_1: pin names not known; wires that end beside it: register_1_q, risc_vprogramrom_1_p2
  Multiplexer #(.width(32), .enable("false")) multiplexer_2 (
    .in0(risc_vprogramrom_1_p2), .in1(zapinst_1_nopinst), .out(multiplexer_2_out), .sel(or_1_out));
  Register #(.width(32)) PC (.D(register_1_q), .clk(clk), .Q(PC_q));  // open: en, clr
  ZapInst zapinst_1 (.Zap(or_1_out), .Nopinst(zapinst_1_nopinst));
  Multiplexer #(.width(32), .enable("false")) multiplexer_3 (
    .in0(IF_DE_instr_q), .in1(zapinst_1_nopinst), .out(multiplexer_3_out), .sel(or_1_out));
  not not_1 (not_1_out, clk);
  Decode decode_1 (
    .instr(multiplexer_3_out), .rs1(decode_1_rs1), .rs2(decode_1_rs2), .rd(decode_1_rd), .imm(decode_1_imm),
    .useImm(decode_1_useimm), .ALUop(decode_1_aluop), .onehot(decode_1_onehot), .regWE(decode_1_regwe),
    .set(decode_1_set), .shiftbyregval(decode_1_shiftbyregval), .setsign(decode_1_setsign),
    .AUIPC(decode_1_auipc), .ZeroOutA(decode_1_zeroouta));
  // RegisterFile registerfile_1: pin names not known; wires that end beside it: registerfile_1_p1, not_1_out, registerfile_1_p3, registerfile_1_p4, decode_1_rs1, decode_1_rs2, registerfile_1_p7, registerfile_1_p8
  Register #(.width(32)) DE_EX_A (.D(registerfile_1_p7), .clk(clk), .Q(DE_EX_A_q));  // open: en, clr
  Register #(.width(32)) DE_EX_B (.D(registerfile_1_p8), .clk(clk), .Q(DE_EX_B_q));  // open: en, clr
  Register #(.width(5)) rs1 (.D(decode_1_rs1), .clk(clk), .Q(rs1_q));  // open: en, clr
  Register #(.width(5)) rs2 (.D(decode_1_rs2), .clk(clk), .Q(rs2_q));  // open: en, clr
  Register #(.width(5)) DE_EX_rd (.D(decode_1_rd), .clk(clk), .Q(DE_EX_rd_q));  // open: en, clr
  Register #(.width(32)) DE_EX_imm (.D(decode_1_imm), .clk(clk), .Q(DE_EX_imm_q));  // open: en, clr
  Register #(.width(1)) DE_EX_useImm (.D(decode_1_useimm), .clk(clk), .Q(DE_EX_useImm_q));  // open: en, clr
  Register #(.width(4)) DE_EX_ALUop (.D(decode_1_aluop), .clk(clk), .Q(DE_EX_ALUop_q));  // open: en, clr
  Register #(.width(32)) OneHot (.D(decode_1_onehot), .clk(clk), .Q(OneHot_q));  // open: en, clr
  Register #(.width(1)) DE_EX_regWE (.D(decode_1_regwe), .clk(clk), .Q(DE_EX_regWE_q));  // open: en, clr
  Register #(.width(1)) DE_EX_set (.D(decode_1_set), .clk(clk), .Q(DE_EX_set_q));  // open: en, clr
  Register #(.width(1)) DE_EX_shiftreg (.D(decode_1_shiftbyregval), .clk(clk), .Q(DE_EX_shiftreg_q));  // open: en, clr
  Register #(.width(1)) set_signed (.D(decode_1_setsign), .clk(clk), .Q(set_signed_q));  // open: en, clr
  Register #(.width(32)) DE_EX_PC (.D(PC_q), .clk(clk), .Q(DE_EX_PC_q));  // open: en, clr
  Register #(.width(1)) AUIPC (.D(decode_1_auipc), .clk(clk), .Q(AUIPC_q));  // open: en, clr
  Register #(.width(1)) ZeroOutA (.D(decode_1_zeroouta), .clk(clk), .Q(ZeroOutA_q));  // open: en, clr
  // Bypass_Black_Box bypass_black_box_1: pin names not known; wires that end beside it: rs1_q, rs2_q, bypass_black_box_1_p3, bypass_black_box_1_p4, registerfile_1_p3, registerfile_1_p4, bypass_black_box_1_p7, bypass_black_box_1_p8
  or or_1 (or_1_out, OneHot_q[24], OneHot_q[25]);
  or or_2 (or_2_out, AUIPC_q, OneHot_q[24]);
  MUX3to1 mux3to1_1 (
    .out_5(mux3to1_1_out_5), .ME(EX_M_Result_q), .WB(registerfile_1_p1), .EX(DE_EX_A_q),
    .Sel(bypass_black_box_1_p7));
  MUX3to1 mux3to1_2 (
    .out_5(mux3to1_2_out_5), .ME(EX_M_Result_q), .WB(registerfile_1_p1), .EX(DE_EX_B_q),
    .Sel(bypass_black_box_1_p8));
  Multiplexer #(.width(32), .enable("false")) multiplexer_4 (
    .in0(mux3to1_2_out_5), .in1(DE_EX_imm_q), .out(multiplexer_4_out), .sel(DE_EX_useImm_q));
  // Comparator_Black_Box comparator_black_box_1: pin names not known; wires that end beside it: mux3to1_1_out_5, multiplexer_4_out, set_signed_q, comparator_black_box_1_p4
  assign bit_extender_1_out = {{31{1'b0}}, comparator_black_box_1_p4};  // Bit_Extender bit_extender_1
  Execute execute_1 (
    .A(mux3to1_1_out_5), .B(mux3to1_2_out_5), .rB(rs2_q), .imm(DE_EX_imm_q), .useImm(DE_EX_useImm_q),
    .ALUop(DE_EX_ALUop_q), .shiftbyregval(DE_EX_shiftreg_q), .UsePC(or_2_out), .PC(DE_EX_PC_q),
    .ZeroA(ZeroOutA_q), .result(execute_1_result));
  Multiplexer #(.width(32), .enable("false")) multiplexer_5 (
    .in0(execute_1_result), .in1(bit_extender_1_out), .out(multiplexer_5_out), .sel(DE_EX_set_q));
  Multiplexer #(.width(32), .enable("false")) multiplexer_6 (
    .in0(multiplexer_5_out), .in1(DE_EX_PC_q), .out(multiplexer_6_out), .sel(or_1_out));
  Register #(.width(32)) EX_M_Result (.D(multiplexer_6_out), .clk(clk), .Q(EX_M_Result_q));  // open: en, clr
  Register #(.width(5)) EX_M_rd (.D(DE_EX_rd_q), .clk(clk), .Q(bypass_black_box_1_p4));  // open: en, clr
  Register #(.width(1)) EX_M_regWE (.D(DE_EX_regWE_q), .clk(clk), .Q(bypass_black_box_1_p3));  // open: en, clr
  RAM ram_1 ();  // open: addr, data, sel, clk, ld, clr
  Register #(.width(32)) M_W_Result (.D(EX_M_Result_q), .clk(clk), .Q(registerfile_1_p1));  // open: en, clr
  Register #(.width(32)) M_W_Data (.clk(clk));  // open: D, en, Q, clr
  Register #(.width(1)) M_W_regWE (.D(bypass_black_box_1_p3), .clk(clk), .Q(registerfile_1_p3));  // open: en, clr
  Register #(.width(5)) M_W_rd (.D(bypass_black_box_1_p4), .clk(clk), .Q(registerfile_1_p4));  // open: en, clr

  // Notes on the sheet:
  //   Notes:
  //   not to force you into using a template
  //   This is a working circuit for all of the table A instructions
  //   - Feel free to change the structure of this for any reason
  //   as it is to save you from repeating work you've done,
  //   - Behavior for table B instructions is undefined in this release circuit
  //   - This should pass the sanity check if you submit it as is
  //   contents of risc_vprogramrom_1 (hex, n*v repeats v):
  //   Addi x1,x1,4 Addi x1,x1,4 Addi x1,x1,4 Jalr x2, x4,16 Addi x2,x2, 1 Addi x3,x3,1 Addi x4, x4,1 Addi
  //   x6,x6,1 Addi x7,x7,1 Addi x8,x8,1
  //   go for it!
  //   The amount of registers between decode
  //   and execute is for readability. If you
  //   do want to combine them into less registers,
  //   Register Write Enable
  //   Okay to leave
  //   these outputs unused
  //   passes with the release circuit
  //   RAM is only here so that the autograder lite
endmodule

module Fetching (
  input  clk,
  output [31:0] intr
);

  wire [31:0] increment_pc_1_out_2, register_1_q;

  Register #(.width(32), .trigger("falling")) register_1 (
    .D(increment_pc_1_out_2), .clk(clk), .Q(register_1_q));  // open: en, clr
  Increment_PC increment_pc_1 (.in_1(register_1_q), .out_2(increment_pc_1_out_2));
endmodule

module Increment_PC (
  input  [31:0] in_1,
  output [31:0] out_2
);

  // Incrementer #(.width(30)) incrementer_1: pin names not known; wires that end beside it: in_1[31:2], out_2[31:2]

  assign out_2[1:0] = in_1[1:0];
endmodule

module Decode (
  input  [31:0] instr,
  output [4:0] rs1,
  output [4:0] rs2,
  output [4:0] rd,
  output [31:0] imm,
  output useImm,
  output [3:0] ALUop,
  output [31:0] onehot,
  output regWE,
  output set,
  output shiftbyregval,
  output setsign,
  output AUIPC,
  output ZeroOutA
);

  wire or_1_out, or_5_out;
  wire [3:3] decode_black_box_1_p7;
  wire [31:0] decode_black_box_1_p5, jalimm_1_jumpimm;

  // Decode_Black_Box decode_black_box_1: pin names not known; wires that end beside it: instr, rs1, rs2, rd, decode_black_box_1_p5, useImm, {decode_black_box_1_p7[3], ALUop[2:0]}, onehot[0], onehot[1], onehot[2], onehot[3], onehot[4], onehot[5], onehot[6], onehot[7], onehot[8], onehot[9], onehot[10], onehot[11], onehot[12], onehot[13], onehot[14], onehot[15], onehot[16], onehot[17], onehot[18], onehot[19], onehot[20], onehot[21], onehot[22], onehot[23], onehot[24], onehot[25], onehot[26], onehot[27], onehot[28], onehot[29], onehot[30]
  or or_1 (or_1_out, instr[4], ~instr[5]);  // OR_Gate
  or or_2 (set, onehot[13], onehot[12], onehot[11], onehot[10]);
  or or_3 (shiftbyregval, onehot[14], onehot[16], onehot[18]);
  or or_4 (setsign, onehot[11], onehot[10]);
  JALimm jalimm_1 (.imm(decode_black_box_1_p5), .Jalctrl(onehot[24]), .Jumpimm(jalimm_1_jumpimm));
  or or_5 (or_5_out, onehot[24], onehot[25]);
  Multiplexer #(.width(32), .enable("false")) multiplexer_1 (
    .in0(decode_black_box_1_p5), .in1(jalimm_1_jumpimm), .out(imm), .sel(or_5_out));
  or or_6 (AUIPC, onehot[24], onehot[21]);
  or or_7 (ALUop[3], decode_black_box_1_p7[3], or_5_out);
  or or_8 (regWE, onehot[24], or_1_out);

  assign ZeroOutA = onehot[20];

  // Notes on the sheet:
  //   Feel free to output the 1 hot if you want!
  //   Example of different ways to decode using what's given
endmodule

module Execute (
  input  [31:0] A,
  input  [31:0] B,
  input  [4:0] rB,
  input  [31:0] imm,
  input  useImm,
  input  [3:0] ALUop,
  input  shiftbyregval,
  input  UsePC,
  input  [31:0] PC,
  input  ZeroA,
  output [31:0] result
);

  wire not_1_out;
  wire [4:0] multiplexer_3_out;
  wire [31:0] and_1_out, bit_extender_1_out, multiplexer_1_out, multiplexer_2_out, multiplexer_4_out;

  not not_1 (not_1_out, ZeroA);
  assign bit_extender_1_out = {{31{not_1_out}}, not_1_out};  // Bit_Extender bit_extender_1
  Multiplexer #(.width(32), .enable("false")) multiplexer_1 (.in0(B), .in1(imm), .out(multiplexer_1_out), .sel(useImm));
  Multiplexer #(.width(32), .enable("false")) multiplexer_2 (
    .in0(multiplexer_1_out), .in1(A), .out(multiplexer_2_out), .sel(shiftbyregval));
  Multiplexer #(.width(5), .enable("false")) multiplexer_3 (
    .in0(rB), .in1(B[4:0]), .out(multiplexer_3_out), .sel(shiftbyregval));
  Multiplexer #(.width(32), .enable("false")) multiplexer_4 (.in0(A), .in1(PC), .out(multiplexer_4_out), .sel(UsePC));
  assign and_1_out = multiplexer_4_out & bit_extender_1_out;  // AND_Gate and_1, 32 bits wide
  // ALU alu_1: pin names not known; wires that end beside it: and_1_out, multiplexer_2_out, ALUop, multiplexer_3_out, result
endmodule

module MUX3to1 (
  input  [1:0] Sel,
  input  [31:0] EX,
  input  [31:0] WB,
  input  [31:0] ME,
  output [31:0] out_5
);

  wire [31:0] multiplexer_1_out;

  Multiplexer #(.width(32), .enable("false")) multiplexer_1 (.in0(EX), .in1(WB), .out(multiplexer_1_out), .sel(Sel[0]));
  Multiplexer #(.width(32), .enable("false")) multiplexer_2 (
    .in0(multiplexer_1_out), .in1(ME), .out(out_5), .sel(Sel[1]));
endmodule

module JALimm (
  input  [31:0] imm,
  input  Jalctrl,
  output [31:0] Jumpimm
);

  wire [0:0] not_1_out;
  wire [30:0] bit_extender_2_out;
  wire [31:0] bit_extender_1_out;

  assign bit_extender_1_out = {{20{imm[11]}}, {imm[11:1], Jalctrl}};  // Bit_Extender bit_extender_1
  assign bit_extender_2_out = {{11{imm[31]}}, {imm[31], imm[19:12], imm[20], imm[30:21]}};  // Bit_Extender bit_extender_2
  not not_1 (not_1_out[0], Jalctrl);
  Multiplexer #(.width(32), .enable("false")) multiplexer_1 (
    .in0(bit_extender_1_out), .in1({bit_extender_2_out, not_1_out[0]}), .out(Jumpimm), .sel(Jalctrl));
endmodule

module ZapInst (
  input  Zap,
  output [31:0] Nopinst
);

  wire [3:2] not_1_out;

  not not_1 (not_1_out[2], Zap);
  not not_2 (not_1_out[3], Zap);
  assign Nopinst = {{27{1'b0}}, {Zap, not_1_out, {2{Zap}}}};  // Bit_Extender bit_extender_1
endmodule
