// Logisim project riscv-3.circ as structural Verilog: 6 circuits, main circuit RISCV32
module RISCV32 (
);

  wire AUIPC_q, bypass_black_box_1_p3, clk, comparator_black_box_1_p4, DE_EX_regWE_q, DE_EX_set_q,
       DE_EX_shiftreg_q, DE_EX_useImm_q, decode_1_auipc, decode_1_regwe, decode_1_set, decode_1_setsign,
       decode_1_shiftbyregval, decode_1_useimm, decode_1_zeroouta, not_1_out, registerfile_1_p3,
       set_signed_q, ZeroOutA_q;
  wire [1:0] bypass_black_box_1_p7, bypass_black_box_1_p8;
  wire [3:0] DE_EX_ALUop_q, decode_1_aluop;
  wire [4:0] bypass_black_box_1_p4, DE_EX_rd_q, decode_1_rd, decode_1_rs1, decode_1_rs2, registerfile_1_p4,
       rs1_q, rs2_q;
  wire [31:0] bit_extender_1_out, DE_EX_A_q, DE_EX_B_q, DE_EX_imm_q, DE_EX_PC_q, decode_1_imm, EX_M_Result_q,
       execute_1_result, IF_DE_instr_q, increment_pc_1_out_2, multiplexer_1_out, multiplexer_2_out,
       mux3to1_1_out_5, mux3to1_2_out_5, PC_q, register_1_q, registerfile_1_p1, registerfile_1_p7,
       registerfile_1_p8, risc_vprogramrom_1_p2;

  Clock clock_1 (.out(clk));
  Register #(.width(32)) register_1 (.D(increment_pc_1_out_2), .clk(clk), .Q(register_1_q));  // open: en, clr
  Increment_PC increment_pc_1 (.in_1(register_1_q), .out_2(increment_pc_1_out_2));
  Register #(.width(32)) IF_DE_instr (.D(risc_vprogramrom_1_p2), .clk(clk), .Q(IF_DE_instr_q));  // open: en, clr
  // RISC_VProgramROM risc_vprogramrom_1: pin names not known; wires that end beside it: register_1_q, risc_vprogramrom_1_p2
  Register #(.width(32)) PC (.D(register_1_q), .clk(clk), .Q(PC_q));  // open: en, clr
  not not_1 (not_1_out, clk);
  Decode decode_1 (
    .instr(IF_DE_instr_q), .rs1(decode_1_rs1), .rs2(decode_1_rs2), .rd(decode_1_rd), .imm(decode_1_imm),
    .useImm(decode_1_useimm), .ALUop(decode_1_aluop), .regWE(decode_1_regwe), .set(decode_1_set),
    .shiftbyregval(decode_1_shiftbyregval), .setsign(decode_1_setsign), .AUIPC(decode_1_auipc),
    .ZeroOutA(decode_1_zeroouta));
  // RegisterFile registerfile_1: pin names not known; wires that end beside it: registerfile_1_p1, not_1_out, registerfile_1_p3, registerfile_1_p4, decode_1_rs1, decode_1_rs2, registerfile_1_p7, registerfile_1_p8
  Register #(.width(32)) DE_EX_A (.D(registerfile_1_p7), .clk(clk), .Q(DE_EX_A_q));  // open: en, clr
  Register #(.width(32)) DE_EX_B (.D(registerfile_1_p8), .clk(clk), .Q(DE_EX_B_q));  // open: en, clr
  Register #(.width(5)) rs1 (.D(decode_1_rs1), .clk(clk), .Q(rs1_q));  // open: en, clr
  Register #(.width(5)) rs2 (.D(decode_1_rs2), .clk(clk), .Q(rs2_q));  // open: en, clr
  Register #(.width(5)) DE_EX_rd (.D(decode_1_rd), .clk(clk), .Q(DE_EX_rd_q));  // open: en, clr
  Register #(.width(32)) DE_EX_imm (.D(decode_1_imm), .clk(clk), .Q(DE_EX_imm_q));  // open: en, clr
  Register #(.width(1)) DE_EX_useImm (.D(decode_1_useimm), .clk(clk), .Q(DE_EX_useImm_q));  // open: en, clr
  Register #(.width(4)) DE_EX_ALUop (.D(decode_1_aluop), .clk(clk), .Q(DE_EX_ALUop_q));  // open: en, clr
  Register #(.width(1)) DE_EX_regWE (.D(decode_1_regwe), .clk(clk), .Q(DE_EX_regWE_q));  // open: en, clr
  Register #(.width(1)) DE_EX_set (.D(decode_1_set), .clk(clk), .Q(DE_EX_set_q));  // open: en, clr
  Register #(.width(1)) DE_EX_shiftreg (.D(decode_1_shiftbyregval), .clk(clk), .Q(DE_EX_shiftreg_q));  // open: en, clr
  Register #(.width(1)) set_signed (.D(decode_1_setsign), .clk(clk), .Q(set_signed_q));  // open: en, clr
  Register #(.width(32)) DE_EX_PC (.D(PC_q), .clk(clk), .Q(DE_EX_PC_q));  // open: en, clr
  Register #(.width(1)) AUIPC (.D(decode_1_auipc), .clk(clk), .Q(AUIPC_q));  // open: en, clr
  Register #(.width(1)) ZeroOutA (.D(decode_1_zeroouta), .clk(clk), .Q(ZeroOutA_q));  // open: en, clr
  // Bypass_Black_Box bypass_black_box_1: pin names not known; wires that end beside it: rs1_q, rs2_q, bypass_black_box_1_p3, bypass_black_box_1_p4, registerfile_1_p3, registerfile_1_p4, bypass_black_box_1_p7, bypass_black_box_1_p8
  MUX3to1 mux3to1_1 (
    .EX(DE_EX_A_q), .out_5(mux3to1_1_out_5), .WB(registerfile_1_p1), .ME(EX_M_Result_q),
    .Sel(bypass_black_box_1_p7));
  MUX3to1 mux3to1_2 (
    .EX(DE_EX_B_q), .out_5(mux3to1_2_out_5), .WB(registerfile_1_p1), .ME(EX_M_Result_q),
    .Sel(bypass_black_box_1_p8));
  Multiplexer #(.width(32), .enable("false")) multiplexer_1 (
    .in0(mux3to1_2_out_5), .in1(DE_EX_imm_q), .out(multiplexer_1_out), .sel(DE_EX_useImm_q));
  // Comparator_Black_Box comparator_black_box_1: pin names not known; wires that end beside it: mux3to1_1_out_5, multiplexer_1_out, set_signed_q, comparator_black_box_1_p4
  assign bit_extender_1_out = {{31{1'b0}}, comparator_black_box_1_p4};  // Bit_Extender bit_extender_1
  Execute execute_1 (
    .A(mux3to1_1_out_5), .B(mux3to1_2_out_5), .rB(rs2_q), .imm(DE_EX_imm_q), .useImm(DE_EX_useImm_q),
    .ALUop(DE_EX_ALUop_q), .shiftbyregval(DE_EX_shiftreg_q), .UsePC(AUIPC_q), .PC(DE_EX_PC_q),
    .ZeroA(ZeroOutA_q), .result(execute_1_result));
  Multiplexer #(.width(32), .enable("false")) multiplexer_2 (
    .in0(execute_1_result), .in1(bit_extender_1_out), .out(multiplexer_2_out), .sel(DE_EX_set_q));
  Register #(.width(32)) EX_M_Result (.D(multiplexer_2_out), .clk(clk), .Q(EX_M_Result_q));  // open: en, clr
  Register #(.width(5)) EX_M_rd (.D(DE_EX_rd_q), .clk(clk), .Q(bypass_black_box_1_p4));  // open: en, clr
  Register #(.width(1)) EX_M_regWE (.D(DE_EX_regWE_q), .clk(clk), .Q(bypass_black_box_1_p3));  // open: en, clr
  RAM ram_1 ();  // open: addr, data, sel, clk, ld, clr
  Register #(.width(32)) M_W_Result (.D(EX_M_Result_q), .clk(clk), .Q(registerfile_1_p1));  // open: en, clr
  Register #(.width(32)) M_W_Data (.clk(clk));  // open: D, en, Q, clr
  Register #(.width(1)) M_W_regWE (.D(bypass_black_box_1_p3), .clk(clk), .Q(registerfile_1_p3));  // open: en, clr
  Register #(.width(5)) M_W_rd (.D(bypass_black_box_1_p4), .clk(clk), .Q(registerfile_1_p4));  // open: en, clr

  // Notes on the sheet:
  //   Notes:
  //   not to force you into using a template
  //   This is a working circuit for all of the table A instructions
  //   - Feel free to change the structure of this for any reason
  //   as it is to save you from repeating work you've done,
  //   - Behavior for table B instructions is undefined in this release circuit
  //   - This should pass the sanity check if you submit it as is
  //   go for it!
  //   The amount of registers between decode
  //   and execute is for readability. If you
  //   do want to combine them into less registers,
  //   Register Write Enable
  //   Okay to leave
  //   these outputs unused
  //   passes with the release circuit
  //   RAM is only here so that the autograder lite
endmodule

module Fetching (
  input  clk,
  output [31:0] intr
);

  wire [31:0] increment_pc_1_out_2, register_1_q;

  Register #(.width(32), .trigger("falling")) register_1 (
    .D(increment_pc_1_out_2), .clk(clk), .Q(register_1_q));  // open: en, clr
  Increment_PC increment_pc_1 (.in_1(register_1_q), .out_2(increment_pc_1_out_2));
endmodule

module Increment_PC (
  input  [31:0] in_1,
  output [31:0] out_2
);

  // Incrementer #(.width(30)) incrementer_1: pin names not known; wires that end beside it: in_1[31:2], out_2[31:2]

  assign out_2[1:0] = in_1[1:0];
endmodule

module Decode (
  input  [31:0] instr,
  output [4:0] rs1,
  output [4:0] rs2,
  output [4:0] rd,
  output [31:0] imm,
  output useImm,
  output [3:0] ALUop,
  output regWE,
  output set,
  output shiftbyregval,
  output setsign,
  output AUIPC,
  output ZeroOutA
);

  wire [30:0] decode_black_box_1_p8;

  // Decode_Black_Box decode_black_box_1: pin names not known; wires that end beside it: instr, rs1, rs2, rd, imm, useImm, ALUop, decode_black_box_1_p8[0], decode_black_box_1_p8[1], decode_black_box_1_p8[2], decode_black_box_1_p8[3], decode_black_box_1_p8[4], decode_black_box_1_p8[5], decode_black_box_1_p8[6], decode_black_box_1_p8[7], decode_black_box_1_p8[8], decode_black_box_1_p8[9], decode_black_box_1_p8[10], decode_black_box_1_p8[11], decode_black_box_1_p8[12], decode_black_box_1_p8[13], decode_black_box_1_p8[14], decode_black_box_1_p8[15], decode_black_box_1_p8[16], decode_black_box_1_p8[17], decode_black_box_1_p8[18], decode_black_box_1_p8[19], ZeroOutA, AUIPC, decode_black_box_1_p8[22], decode_black_box_1_p8[23], decode_black_box_1_p8[24], decode_black_box_1_p8[25], decode_black_box_1_p8[26], decode_black_box_1_p8[27], decode_black_box_1_p8[28], decode_black_box_1_p8[29], decode_black_box_1_p8[30]
  or or_1 (regWE, instr[4], ~instr[5]);  // OR_Gate
  or or_2 (set, decode_black_box_1_p8[13], decode_black_box_1_p8[12], decode_black_box_1_p8[11], decode_black_box_1_p8[10]);
  or or_3 (shiftbyregval, decode_black_box_1_p8[14], decode_black_box_1_p8[16], decode_black_box_1_p8[18]);
  or or_4 (setsign, decode_black_box_1_p8[11], decode_black_box_1_p8[10]);

  // Notes on the sheet:
  //   Feel free to output the 1 hot if you want!
  //   Example of different ways to decode using what's given
endmodule

module Execute (
  input  [31:0] A,
  input  [31:0] B,
  input  [4:0] rB,
  input  [31:0] imm,
  input  useImm,
  input  [3:0] ALUop,
  input  shiftbyregval,
  input  UsePC,
  input  [31:0] PC,
  input  ZeroA,
  output [31:0] result
);

  wire not_1_out;
  wire [4:0] multiplexer_3_out;
  wire [31:0] and_1_out, bit_extender_1_out, multiplexer_1_out, multiplexer_2_out, multiplexer_4_out;

  not not_1 (not_1_out, ZeroA);
  assign bit_extender_1_out = {{31{not_1_out}}, not_1_out};  // Bit_Extender bit_extender_1
  Multiplexer #(.width(32), .enable("false")) multiplexer_1 (.in0(B), .in1(imm), .out(multiplexer_1_out), .sel(useImm));
  Multiplexer #(.width(32), .enable("false")) multiplexer_2 (
    .in0(multiplexer_1_out), .in1(A), .out(multiplexer_2_out), .sel(shiftbyregval));
  Multiplexer #(.width(5), .enable("false")) multiplexer_3 (
    .in0(rB), .in1(B[4:0]), .out(multiplexer_3_out), .sel(shiftbyregval));
  Multiplexer #(.width(32), .enable("false")) multiplexer_4 (.in0(A), .in1(PC), .out(multiplexer_4_out), .sel(UsePC));
  assign and_1_out = multiplexer_4_out & bit_extender_1_out;  // AND_Gate and_1, 32 bits wide
  // ALU alu_1: pin names not known; wires that end beside it: and_1_out, multiplexer_2_out, ALUop, multiplexer_3_out, result
endmodule

module MUX3to1 (
  input  [1:0] Sel,
  input  [31:0] EX,
  input  [31:0] WB,
  input  [31:0] ME,
  output [31:0] out_5
);

  wire [31:0] multiplexer_1_out;

  Multiplexer #(.width(32), .enable("false")) multiplexer_1 (.in0(EX), .in1(WB), .out(multiplexer_1_out), .sel(Sel[0]));
  Multiplexer #(.width(32), .enable("false")) multiplexer_2 (
    .in0(multiplexer_1_out), .in1(ME), .out(out_5), .sel(Sel[1]));
endmodule
